// Logisim project thinking2.circ as structural Verilog: 1 circuit, main circuit main
module main (
  input  B3,
  input  B2,
  input  B1,
  input  B0,
  output G3,
  output G2,
  output G1,
  output G0
);

  xor xor_1 (G2, B3, B2);
  xor xor_2 (G1, B2, B1);
  xor xor_3 (G0, B1, B0);

  assign G3 = B3;
endmodule
