// Logisim project thinking3.circ as structural Verilog: 1 circuit, main circuit main
module main (
  input  A,
  input  B,
  input  C,
  input  D,
  output \偶校验 ,
  output \奇校验 
);

  ExactlyOne xor_1 (.out(\偶校验 ), .in0(A), .in1(B), .in2(C), .in3(D));
  not not_1 (\奇校验 , \偶校验 );
endmodule
