// Logisim project lab2.4.circ as structural Verilog: 3 circuits, main circuit main
module main (
  input  [6:0] Input,
  input  in_2,
  output [6:0] Output,
  output NoError
);

  wire \n3_8译码器_1_y1_l , \n3_8译码器_1_y2_l , \n3_8译码器_1_y3_l , \n3_8译码器_1_y4_l , \n3_8译码器_1_y5_l ,
       \n3_8译码器_1_y6_l , \n3_8译码器_1_y7_l ;
  wire [2:0] \n4位奇偶校验器_1_even ;

  Hex_Digit_Display hex_digit_display_1 (.value({in_2, \n4位奇偶校验器_1_even }));  // open: dp
  \_4位奇偶校验器  \u_4位奇偶校验器_1  (
    .N0(Input[6]), .N1(Input[4]), .N2(Input[2]), .N3(Input[0]), .EVEN(\n4位奇偶校验器_1_even [0]));  // open: ODD
  \_4位奇偶校验器  \u_4位奇偶校验器_2  (
    .N0(Input[1]), .N1(Input[2]), .N2(Input[5]), .N3(Input[6]), .EVEN(\n4位奇偶校验器_1_even [1]));  // open: ODD
  \_4位奇偶校验器  \u_4位奇偶校验器_3  (
    .N0(Input[3]), .N1(Input[4]), .N2(Input[5]), .N3(Input[6]), .EVEN(\n4位奇偶校验器_1_even [2]));  // open: ODD
  \_3_8译码器  \u_3_8译码器_1  (
    .G1(1'b1), .G2A_L(1'b0), .G2B_L(1'b0), .A(\n4位奇偶校验器_1_even [0]), .B(\n4位奇偶校验器_1_even [1]),
    .C(\n4位奇偶校验器_1_even [2]), .Y0_L(NoError), .Y1_L(\n3_8译码器_1_y1_l ), .Y2_L(\n3_8译码器_1_y2_l ),
    .Y3_L(\n3_8译码器_1_y3_l ), .Y4_L(\n3_8译码器_1_y4_l ), .Y5_L(\n3_8译码器_1_y5_l ), .Y6_L(\n3_8译码器_1_y6_l ),
    .Y7_L(\n3_8译码器_1_y7_l ));
  xor xor_1 (Output[0], Input[0], \n3_8译码器_1_y1_l );
  xor xor_2 (Output[1], Input[1], \n3_8译码器_1_y2_l );
  xor xor_3 (Output[2], Input[2], \n3_8译码器_1_y3_l );
  xor xor_4 (Output[3], Input[3], \n3_8译码器_1_y4_l );
  xor xor_5 (Output[4], Input[4], \n3_8译码器_1_y5_l );
  xor xor_6 (Output[5], Input[5], \n3_8译码器_1_y6_l );
  xor xor_7 (Output[6], Input[6], \n3_8译码器_1_y7_l );
  Hex_Digit_Display hex_digit_display_2 ();  // open: value, dp

  // Notes on the sheet:
  //   输入引脚
  //   输入引脚
  //   请勿修改引脚名称、电路名称及电路封装外观
  //   提示：使用异或门、4位奇偶校验电路和74x138子电路实现7位汉明码纠错电路。
  //   输出引脚
endmodule

module \_3_8译码器  (
  input  G1,
  input  G2A_L,
  input  G2B_L,
  input  A,
  input  B,
  input  C,
  output Y0_L,
  output Y1_L,
  output Y2_L,
  output Y3_L,
  output Y4_L,
  output Y5_L,
  output Y6_L,
  output Y7_L
);

  wire and_1_out, nand_1_out, nand_2_out, nand_3_out, nand_4_out, nand_5_out, nand_6_out, nand_7_out,
       nand_8_out, not_1_out, not_2_out, not_3_out, not_4_out, not_5_out, not_6_out, not_7_out;

  not not_1 (not_1_out, G1);
  and and_1 (and_1_out, ~not_1_out, ~G2A_L, ~G2B_L);  // AND_Gate
  not not_2 (not_2_out, A);
  not not_3 (not_3_out, B);
  not not_4 (not_4_out, C);
  not not_5 (not_5_out, not_2_out);
  not not_6 (not_6_out, not_3_out);
  not not_7 (not_7_out, not_4_out);
  nand nand_1 (nand_1_out, not_2_out, not_3_out, not_4_out, and_1_out);
  not not_8 (Y0_L, nand_1_out);
  not not_9 (Y1_L, nand_2_out);
  nand nand_2 (nand_2_out, not_3_out, not_4_out, not_5_out, and_1_out);
  nand nand_3 (nand_3_out, not_2_out, not_4_out, not_6_out, and_1_out);
  not not_10 (Y2_L, nand_3_out);
  nand nand_4 (nand_4_out, not_4_out, not_5_out, not_6_out, and_1_out);
  not not_11 (Y3_L, nand_4_out);
  nand nand_5 (nand_5_out, not_2_out, not_3_out, not_7_out, and_1_out);
  not not_12 (Y4_L, nand_5_out);
  nand nand_6 (nand_6_out, not_3_out, not_5_out, not_7_out, and_1_out);
  not not_13 (Y5_L, nand_6_out);
  nand nand_7 (nand_7_out, not_2_out, not_6_out, not_7_out, and_1_out);
  not not_14 (Y6_L, nand_7_out);
  not not_15 (Y7_L, nand_8_out);
  nand nand_8 (nand_8_out, not_6_out, and_1_out, not_5_out, not_7_out);

  // Notes on the sheet:
  //   3-8译码器
endmodule

module \_4位奇偶校验器  (
  input  N0,
  input  N1,
  input  N2,
  input  N3,
  output EVEN,
  output ODD
);

  ExactlyOne xor_1 (.out(EVEN), .in0(N0), .in1(N1), .in2(N2), .in3(N3));
  not not_1 (ODD, EVEN);

  // Notes on the sheet:
  //   4位奇偶校验电路
endmodule
