// Logisim project lab2.5.circ as structural Verilog: 2 circuits, main circuit main
module main (
  input  [7:0] DataIn,
  input  [2:0] shamt,
  input  L_R,
  input  A_L,
  output [7:0] DataOut
);

  wire undriven, undriven_3;
  wire [0:0] and_1_out;
  wire [1:0] and_3_out, and_7_out;
  wire [3:0] and_8_out;
  wire [7:0] multiplexer_1_out, multiplexer_2_out;
  wire [7:6] undriven_4;
  wire [7:7] and_2_out, and_4_out, and_6_out, and_12_out, undriven_2;

  and and_1 (and_1_out[0], A_L, DataIn[7]);
  and and_2 (and_2_out[7], DataIn[7], A_L);
  Multiplexer #(.select(2), .width(8), .enable("false")) multiplexer_1 (
    .in0(DataIn), .in1(DataIn), .in2({and_2_out[7], DataIn[7:1]}), .in3({DataIn[6:0], and_1_out[0]}),
    .out(multiplexer_1_out), .sel({shamt[0], L_R}));
  and and_3 (and_3_out[0], A_L, multiplexer_1_out[6]);
  and and_4 (and_4_out[7], undriven_2[7], undriven);
  and and_5 (and_3_out[1], A_L, multiplexer_1_out[7]);
  and and_6 (and_6_out[7], multiplexer_1_out[7], A_L);
  Multiplexer #(.select(2), .width(8), .enable("false")) multiplexer_2 (
    .in0(multiplexer_1_out), .in1(multiplexer_1_out), .in2({{2{and_6_out[7]}}, multiplexer_1_out[7:2]}),
    .in3({multiplexer_1_out[5:0], and_3_out}), .out(multiplexer_2_out), .sel({shamt[1], L_R}));
  and and_7 (and_7_out[0], undriven_3, undriven_4[6]);
  and and_8 (and_8_out[0], A_L, multiplexer_2_out[4]);
  and and_9 (and_7_out[1], undriven_3, undriven_4[7]);
  and and_10 (and_8_out[1], A_L, multiplexer_2_out[5]);
  and and_11 (and_8_out[2], A_L, multiplexer_2_out[6]);
  and and_12 (and_12_out[7], multiplexer_2_out[7], A_L);
  and and_13 (and_8_out[3], A_L, multiplexer_2_out[7]);
  Multiplexer #(.select(2), .width(8), .enable("false")) multiplexer_3 (
    .in0(multiplexer_2_out), .in1(multiplexer_2_out), .in2({{4{and_12_out[7]}}, multiplexer_2_out[7:4]}),
    .in3({multiplexer_2_out[3:0], and_8_out}), .out(DataOut), .sel({shamt[2], L_R}));

  // Other names for the same wires on the sheet: Din[7:0] = DataIn; Left_Right = L_R; Arth_Logic = A_L;
  //   Dout[7:0] = DataOut

  // Notes on the sheet:
  //   in
  //   Arth/Logic
  //   L/R,A/L: 00逻辑右移，01算术右移，10逻辑左移，11：循环左移
  //   输入引脚
  //   1
  //   请勿修改引脚名称、电路名称及电路封装外观
  //   提示：使用多路选择器级联实现8位桶形移位器，禁止直接使用移位器组件。
  //   对选择器，00/01都不移动；10右移，11左移
  //   Arth/Logic
  //   out
  //   输出引脚
  //   2
  //   in
  //   out
  //   4
endmodule

module _32_buck (
  input  [31:0] DataIn,
  input  L_R,
  input  [4:0] shamt,
  input  A_L,
  output [31:0] DataOut
);

  wire [0:0] and_1_out;
  wire [1:0] and_3_out, and_4_out, multiplexer_1_out, multiplexer_1_out_2, multiplexer_1_out_3,
       multiplexer_1_out_4, multiplexer_1_out_5, multiplexer_1_out_6, multiplexer_1_out_7,
       multiplexer_1_out_8, multiplexer_1_out_9, multiplexer_1_out_10, multiplexer_1_out_11,
       multiplexer_1_out_12, multiplexer_1_out_13, multiplexer_1_out_14, multiplexer_1_out_15,
       multiplexer_1_out_16;
  wire [3:0] and_5_out, and_6_out;
  wire [7:0] and_7_out, and_8_out;
  wire [15:0] and_9_out, and_10_out;
  wire [31:0] multiplexer_2_out, multiplexer_3_out, multiplexer_4_out;
  wire [31:31] and_2_out;

  and and_1 (and_1_out[0], A_L, DataIn[31]);
  and and_2 (and_2_out[31], DataIn[31], A_L);
  assign and_3_out = {2{A_L}} & multiplexer_1_out_16;  // AND_Gate and_3, 2 bits wide
  Multiplexer #(.select(2), .width(32), .enable("false")) multiplexer_1 (
    .in0(DataIn), .in1(DataIn), .in2({and_2_out[31], DataIn[31:1]}), .in3({DataIn[30:0], and_1_out[0]}),
    .out({multiplexer_1_out_16, multiplexer_1_out_15, multiplexer_1_out_14, multiplexer_1_out_13, multiplexer_1_out_12, multiplexer_1_out_11, multiplexer_1_out_10, multiplexer_1_out_9, multiplexer_1_out_8, multiplexer_1_out_7, multiplexer_1_out_6, multiplexer_1_out_5, multiplexer_1_out_4, multiplexer_1_out_3, multiplexer_1_out_2, multiplexer_1_out}),
    .sel({shamt[0], L_R}));
  assign and_4_out = multiplexer_1_out_16 & {2{A_L}};  // AND_Gate and_4, 2 bits wide
  Multiplexer #(.select(2), .width(32), .enable("false")) multiplexer_2 (
    .in0({multiplexer_1_out_16, multiplexer_1_out_15, multiplexer_1_out_14, multiplexer_1_out_13, multiplexer_1_out_12, multiplexer_1_out_11, multiplexer_1_out_10, multiplexer_1_out_9, multiplexer_1_out_8, multiplexer_1_out_7, multiplexer_1_out_6, multiplexer_1_out_5, multiplexer_1_out_4, multiplexer_1_out_3, multiplexer_1_out_2, multiplexer_1_out}),
    .in1({multiplexer_1_out_16, multiplexer_1_out_15, multiplexer_1_out_14, multiplexer_1_out_13, multiplexer_1_out_12, multiplexer_1_out_11, multiplexer_1_out_10, multiplexer_1_out_9, multiplexer_1_out_8, multiplexer_1_out_7, multiplexer_1_out_6, multiplexer_1_out_5, multiplexer_1_out_4, multiplexer_1_out_3, multiplexer_1_out_2, multiplexer_1_out}),
    .in2({and_4_out, multiplexer_1_out_16, multiplexer_1_out_15, multiplexer_1_out_14, multiplexer_1_out_13, multiplexer_1_out_12, multiplexer_1_out_11, multiplexer_1_out_10, multiplexer_1_out_9, multiplexer_1_out_8, multiplexer_1_out_7, multiplexer_1_out_6, multiplexer_1_out_5, multiplexer_1_out_4, multiplexer_1_out_3, multiplexer_1_out_2}),
    .in3({multiplexer_1_out_15, multiplexer_1_out_14, multiplexer_1_out_13, multiplexer_1_out_12, multiplexer_1_out_11, multiplexer_1_out_10, multiplexer_1_out_9, multiplexer_1_out_8, multiplexer_1_out_7, multiplexer_1_out_6, multiplexer_1_out_5, multiplexer_1_out_4, multiplexer_1_out_3, multiplexer_1_out_2, multiplexer_1_out, and_3_out}),
    .out(multiplexer_2_out), .sel({shamt[1], L_R}));
  assign and_5_out = {4{A_L}} & multiplexer_2_out[31:28];  // AND_Gate and_5, 4 bits wide
  assign and_6_out = multiplexer_2_out[31:28] & {4{A_L}};  // AND_Gate and_6, 4 bits wide
  Multiplexer #(.select(2), .width(32), .enable("false")) multiplexer_3 (
    .in0(multiplexer_2_out), .in1(multiplexer_2_out), .in2({and_6_out, multiplexer_2_out[31:4]}),
    .in3({multiplexer_2_out[27:0], and_5_out}), .out(multiplexer_3_out), .sel({shamt[2], L_R}));
  assign and_7_out = {8{A_L}} & multiplexer_3_out[31:24];  // AND_Gate and_7, 8 bits wide
  assign and_8_out = multiplexer_3_out[31:24] & {8{A_L}};  // AND_Gate and_8, 8 bits wide
  Multiplexer #(.select(2), .width(32), .enable("false")) multiplexer_4 (
    .in0(multiplexer_3_out), .in1(multiplexer_3_out), .in2({and_8_out, multiplexer_3_out[31:8]}),
    .in3({multiplexer_3_out[23:0], and_7_out}), .out(multiplexer_4_out), .sel({shamt[3], L_R}));
  assign and_9_out = {16{A_L}} & multiplexer_4_out[31:16];  // AND_Gate and_9, 16 bits wide
  assign and_10_out = multiplexer_4_out[31:16] & {16{A_L}};  // AND_Gate and_10, 16 bits wide
  Multiplexer #(.select(2), .width(32), .enable("false")) multiplexer_5 (
    .in0(multiplexer_4_out), .in1(multiplexer_4_out), .in2({and_10_out, multiplexer_4_out[31:16]}),
    .in3({multiplexer_4_out[15:0], and_9_out}), .out(DataOut), .sel({shamt[4], L_R}));

  // Other names for the same wires on the sheet: Din[31:0] = DataIn; Arth_Logic = A_L; Left_Right = L_R;
  //   Dout[31:0] = DataOut

  // Notes on the sheet:
  //   L/R,A/L: 00逻辑右移，01算术右移，10逻辑左移，11：循环左移
  //   输入引脚
  //   请勿修改引脚名称、电路名称及电路封装外观
  //   提示：使用多路选择器级联实现8位桶形移位器，禁止直接使用移位器组件。
  //   输出引脚
  //   1
  //   对选择器，00/01都不移动；10右移，11左移
  //   2
  //   4
  //   8
  //   16
endmodule
