// Logisim project lab3.1.circ as structural Verilog: 2 circuits, main circuit CNTR4U
module CNTR4U (
  input  CLK,
  input  LD,
  input  CLR,
  input  D0,
  input  D1,
  input  D2,
  input  D3,
  input  ENP,
  input  ENT,
  output Q0,
  output Q1,
  output Q2,
  output Q3,
  output RCO
);

  wire and_1_out, and_2_out, and_3_out, and_4_out, and_5_out, and_6_out, and_7_out, and_8_out, and_10_out,
       and_11_out, and_12_out, and_13_out, and_14_out, and_15_out, and_16_out, and_17_out, buffer_1_out,
       d_ff_1_qn, d_ff_2_qn, d_ff_3_qn, d_ff_4_qn, not_1_out, not_2_out, not_3_out, or_1_out, or_2_out,
       or_3_out, or_4_out, xor_1_out, xor_2_out, xor_3_out, xor_4_out;

  buf buffer_1 (buffer_1_out, CLR);
  not not_1 (not_1_out, d_ff_1_qn);
  and and_1 (and_1_out, ~d_ff_1_qn, ~d_ff_2_qn);  // AND_Gate
  and and_2 (and_2_out, ~d_ff_1_qn, ~d_ff_2_qn, ~d_ff_3_qn);  // AND_Gate
  and and_3 (and_3_out, ENP, ENT);
  not not_2 (not_2_out, CLK);
  and and_4 (and_4_out, LD, ~buffer_1_out);  // AND_Gate
  and and_5 (and_5_out, ~and_4_out, ~buffer_1_out);  // AND_Gate
  and and_6 (and_6_out, not_1_out, and_3_out);
  and and_7 (and_7_out, and_1_out, and_3_out);
  and and_8 (and_8_out, and_2_out, and_3_out);
  not not_3 (not_3_out, ENT);
  xor xor_1 (xor_1_out, and_3_out, ~d_ff_1_qn);  // XOR_Gate
  xor xor_2 (xor_2_out, and_6_out, ~d_ff_2_qn);  // XOR_Gate
  xor xor_3 (xor_3_out, and_7_out, ~d_ff_3_qn);  // XOR_Gate
  xor xor_4 (xor_4_out, and_8_out, ~d_ff_4_qn);  // XOR_Gate
  and and_9 (RCO, ~d_ff_4_qn, ~not_3_out, ~d_ff_3_qn, ~d_ff_2_qn, ~d_ff_1_qn);  // AND_Gate
  and and_10 (and_10_out, and_4_out, D0);
  and and_11 (and_11_out, and_5_out, xor_1_out);
  and and_12 (and_12_out, and_4_out, D1);
  and and_13 (and_13_out, and_5_out, xor_2_out);
  and and_14 (and_14_out, and_4_out, D2);
  and and_15 (and_15_out, and_5_out, xor_3_out);
  and and_16 (and_16_out, and_4_out, D3);
  and and_17 (and_17_out, and_5_out, xor_4_out);
  or or_1 (or_1_out, and_10_out, and_11_out);
  or or_2 (or_2_out, and_12_out, and_13_out);
  or or_3 (or_3_out, and_14_out, and_15_out);
  or or_4 (or_4_out, and_16_out, and_17_out);
  D_Flip_Flop #(.trigger("falling")) d_ff_1 (
    .clk(not_2_out), .D(or_1_out), .Q(Q0), .Qn(d_ff_1_qn));  // open: preset, reset
  D_Flip_Flop #(.trigger("falling")) d_ff_2 (
    .clk(not_2_out), .D(or_2_out), .Q(Q1), .Qn(d_ff_2_qn));  // open: preset, reset
  D_Flip_Flop #(.trigger("falling")) d_ff_3 (
    .clk(not_2_out), .D(or_3_out), .Q(Q2), .Qn(d_ff_3_qn));  // open: preset, reset
  D_Flip_Flop #(.trigger("falling")) d_ff_4 (
    .clk(not_2_out), .D(or_4_out), .Q(Q3), .Qn(d_ff_4_qn));  // open: preset, reset

  // Notes on the sheet:
  //   输入引脚
  //   请勿修改引脚名称、电路名称及电路封装外观
  //   提示：使用独立逻辑门实现4位二进制同步计数器，禁止直接使用计数器组件。
  //   输出引脚
endmodule

module rand_8 (
  input  [7:0] in_1,
  input  in_2,
  output [7:0] out_3
);

  wire cntr4u_1_q0, cntr4u_1_q1, cntr4u_1_q2, cntr4u_1_q3, cntr4u_2_q0, cntr4u_2_q3, cntr4u_2_rco, not_2_out,
       not_4_out, xor_1_out, xor_3_out;
  wire [7:0] register_1_q;

  Register #(.Select("low")) register_1 (
    .D(out_3), .en(1'b1), .Q(register_1_q), .clk(in_2), .clr(1'b0), .preset(1'b0));  // open: cs
  not not_1 (out_3[4], not_4_out);
  not not_2 (not_2_out, register_1_q[0]);
  CNTR4U cntr4u_1 (
    .CLK(in_2), .LD(1'b0), .CLR(1'b0), .Q0(cntr4u_1_q0), .Q1(cntr4u_1_q1), .D0(not_2_out),
    .D1(register_1_q[1]), .D2(register_1_q[2]), .Q2(cntr4u_1_q2), .Q3(cntr4u_1_q3), .D3(register_1_q[3]),
    .ENP(1'b1), .ENT(1'b1));  // open: RCO
  CNTR4U cntr4u_2 (
    .CLK(in_2), .LD(1'b0), .CLR(1'b0), .Q0(cntr4u_2_q0), .Q1(out_3[1]), .D0(register_1_q[4]),
    .D1(register_1_q[5]), .D2(register_1_q[6]), .Q2(out_3[2]), .Q3(cntr4u_2_q3), .D3(register_1_q[7]),
    .ENP(1'b1), .ENT(1'b1), .RCO(cntr4u_2_rco));
  Hex_Digit_Display hex_digit_display_1 (.value(out_3[3:0]));  // open: dp
  xor xor_1 (xor_1_out, cntr4u_2_q0, out_3[2]);
  xor xor_2 (out_3[5], cntr4u_1_q0, cntr4u_2_rco);
  Hex_Digit_Display hex_digit_display_2 (.value(out_3[7:4]));  // open: dp
  not not_3 (out_3[0], xor_1_out);
  xor xor_3 (xor_3_out, cntr4u_1_q0, cntr4u_1_q1);
  or or_1 (out_3[7], cntr4u_1_q0, ~cntr4u_1_q3);  // OR_Gate
  nand nand_1 (out_3[3], cntr4u_2_q3, out_3[1], cntr4u_1_q0);
  not not_4 (not_4_out, xor_3_out);
  ExactlyOne xor_4 (.out(out_3[6]), .in0(out_3[7]), .in1(cntr4u_1_q2), .in2(not_4_out));

  // Other names for the same wires on the sheet: CLK = in_2; In[7:0] = in_1; Out[7:0] = out_3
endmodule
