// Logisim project lab3.3.circ as structural Verilog: 7 circuits, main circuit main
module main (
  input  CLK,
  input  [3:0] X,
  input  [3:0] Y,
  input  Reset,
  output [7:0] Prod
);

  wire adder4b_1_cout, LOAD, not_1_out, STOP;
  wire [3:0] \_4位同步计数器_q0 , adder4b_1_f, multiplexer_1_out, multiplexer_2_out;
  wire [7:0] \桶形移位器_dataout ;

  Multiplexer #(.width(4), .enable("false")) multiplexer_1 (
    .in0(4'b0000), .in1(X), .out(multiplexer_1_out), .sel(Prod[0]));
  Hex_Digit_Display hex_digit_display_1 (.value(X));  // open: dp
  not not_1 (not_1_out, STOP);
  ADDER4b adder4b_1 (.X(Prod[7:4]), .Y(multiplexer_1_out), .F(adder4b_1_f), .Cout(adder4b_1_cout), .Cin(1'b0));
  Hex_Digit_Display hex_digit_display_2 (.value(Y));  // open: dp
  Register #(.width(4), .Select("low")) register_1 (
    .D(\桶形移位器_dataout [7:4]), .en(not_1_out), .Q(Prod[7:4]), .clk(CLK), .clr(Reset));
  Hex_Digit_Display hex_digit_display_3 (.value(Prod[7:4]));  // open: dp
  // Probe on Prod[7:4]
  BarrelSFT8b \u_桶形移位器  (
    .DataIn({adder4b_1_f, Prod[3:0]}), .shamt(3'b001), .L_R(1'b0), .A_L(1'b0), .DataOut(\桶形移位器_dataout ),
    .IN(adder4b_1_cout));
  Hex_Digit_Display hex_digit_display_4 (.value(Prod[3:0]));  // open: dp
  // Probe on Prod[3:0]
  Register #(.width(4), .Select("low")) Y_2 (
    .D(multiplexer_2_out), .en(not_1_out), .Q(Prod[3:0]), .clk(CLK), .clr(Reset));
  Multiplexer #(.width(4), .enable("false")) multiplexer_2 (
    .in0(\桶形移位器_dataout [3:0]), .in1(Y), .out(multiplexer_2_out), .sel(LOAD));
  // Probe on X
  // Probe on Y
  // Probe on Prod
  CNTR4U \_4位同步计数器  (
    .CLK(CLK), .LD(1'b0), .CLR(Reset), .Q0(\_4位同步计数器_q0 [0]), .Q1(\_4位同步计数器_q0 [1]), .Q2(\_4位同步计数器_q0 [2]),
    .Q3(\_4位同步计数器_q0 [3]), .ENP(not_1_out), .ENT(not_1_out));  // open: D0, D1, D2, D3, RCO
  Hex_Digit_Display hex_digit_display_5 (.value(\_4位同步计数器_q0 ));  // open: dp
  Comparator #(.width(4)) comparator_1 (.a(\_4位同步计数器_q0 ), .b(4'b0000), .eq(LOAD));  // open: gt, lt
  Comparator #(.width(4)) comparator_2 (.a(\_4位同步计数器_q0 ), .b(4'b0101), .eq(STOP));  // open: gt, lt

  // Other names for the same wires on the sheet: RST = Reset; Z[7:0] = Prod

  // Notes on the sheet:
  //   X
  //   输入引脚
  //   P
  //   =
  //   请勿修改引脚名称、电路名称及电路封装外观
  //   提示: 采用无符号数一位乘法实现4位二进制乘法器，禁止直接使用乘法器组件
  //   ×
  //   =
  //   输出引脚
endmodule

module CNTR4U (
  input  CLK,
  input  LD,
  input  CLR,
  input  D0,
  input  D1,
  input  D2,
  input  D3,
  input  ENP,
  input  ENT,
  output Q0,
  output Q1,
  output Q2,
  output Q3,
  output RCO
);

  wire and_1_out, and_2_out, and_3_out, and_4_out, and_5_out, and_6_out, and_7_out, and_8_out, and_10_out,
       and_11_out, and_12_out, and_13_out, and_14_out, and_15_out, and_16_out, and_17_out, buffer_1_out,
       d_ff_1_qn, d_ff_2_qn, d_ff_3_qn, d_ff_4_qn, not_1_out, not_2_out, not_3_out, or_1_out, or_2_out,
       or_3_out, or_4_out, xor_1_out, xor_2_out, xor_3_out, xor_4_out;

  buf buffer_1 (buffer_1_out, CLR);
  not not_1 (not_1_out, d_ff_1_qn);
  and and_1 (and_1_out, ~d_ff_1_qn, ~d_ff_2_qn);  // AND_Gate
  and and_2 (and_2_out, ~d_ff_1_qn, ~d_ff_2_qn, ~d_ff_3_qn);  // AND_Gate
  and and_3 (and_3_out, ENP, ENT);
  not not_2 (not_2_out, CLK);
  and and_4 (and_4_out, LD, ~buffer_1_out);  // AND_Gate
  and and_5 (and_5_out, ~and_4_out, ~buffer_1_out);  // AND_Gate
  and and_6 (and_6_out, not_1_out, and_3_out);
  and and_7 (and_7_out, and_1_out, and_3_out);
  and and_8 (and_8_out, and_2_out, and_3_out);
  not not_3 (not_3_out, ENT);
  xor xor_1 (xor_1_out, and_3_out, ~d_ff_1_qn);  // XOR_Gate
  xor xor_2 (xor_2_out, and_6_out, ~d_ff_2_qn);  // XOR_Gate
  xor xor_3 (xor_3_out, and_7_out, ~d_ff_3_qn);  // XOR_Gate
  xor xor_4 (xor_4_out, and_8_out, ~d_ff_4_qn);  // XOR_Gate
  and and_9 (RCO, ~d_ff_4_qn, ~not_3_out, ~d_ff_3_qn, ~d_ff_2_qn, ~d_ff_1_qn);  // AND_Gate
  and and_10 (and_10_out, and_4_out, D0);
  and and_11 (and_11_out, and_5_out, xor_1_out);
  and and_12 (and_12_out, and_4_out, D1);
  and and_13 (and_13_out, and_5_out, xor_2_out);
  and and_14 (and_14_out, and_4_out, D2);
  and and_15 (and_15_out, and_5_out, xor_3_out);
  and and_16 (and_16_out, and_4_out, D3);
  and and_17 (and_17_out, and_5_out, xor_4_out);
  or or_1 (or_1_out, and_10_out, and_11_out);
  or or_2 (or_2_out, and_12_out, and_13_out);
  or or_3 (or_3_out, and_14_out, and_15_out);
  or or_4 (or_4_out, and_16_out, and_17_out);
  D_Flip_Flop #(.trigger("falling")) d_ff_1 (
    .clk(not_2_out), .D(or_1_out), .Q(Q0), .Qn(d_ff_1_qn));  // open: preset, reset
  D_Flip_Flop #(.trigger("falling")) d_ff_2 (
    .clk(not_2_out), .D(or_2_out), .Q(Q1), .Qn(d_ff_2_qn));  // open: preset, reset
  D_Flip_Flop #(.trigger("falling")) d_ff_3 (
    .clk(not_2_out), .D(or_3_out), .Q(Q2), .Qn(d_ff_3_qn));  // open: preset, reset
  D_Flip_Flop #(.trigger("falling")) d_ff_4 (
    .clk(not_2_out), .D(or_4_out), .Q(Q3), .Qn(d_ff_4_qn));  // open: preset, reset

  // Notes on the sheet:
  //   输入引脚
  //   请勿修改引脚名称、电路名称及电路封装外观
  //   提示：使用独立逻辑门实现4位二进制同步计数器，禁止直接使用计数器组件。
  //   输出引脚
endmodule

module ADDER4b (
  input  [3:0] X,
  input  [3:0] Y,
  input  Cin,
  output [3:0] F,
  output Cout
);

  wire fa_1_cout, fa_2_cout, fa_3_cout;
  wire [3:0] bit_extender_1_out, xor_1_out;

  assign bit_extender_1_out = {{3{Cin}}, Cin};  // Bit_Extender bit_extender_1
  Hex_Digit_Display hex_digit_display_1 (.value(X), .dp(1'b0));
  assign xor_1_out = bit_extender_1_out ^ Y;  // XOR_Gate xor_1, 4 bits wide
  Hex_Digit_Display hex_digit_display_2 (.value(xor_1_out), .dp(1'b0));
  FA fa_1 (.A(X[0]), .B(xor_1_out[0]), .Cin(Cin), .F(F[0]), .Cout(fa_1_cout));
  Hex_Digit_Display hex_digit_display_3 (.value(F), .dp(1'b0));
  FA fa_2 (.A(X[1]), .B(xor_1_out[1]), .Cin(fa_1_cout), .F(F[1]), .Cout(fa_2_cout));
  FA fa_3 (.A(X[2]), .B(xor_1_out[2]), .Cin(fa_2_cout), .F(F[2]), .Cout(fa_3_cout));
  FA fa_4 (.A(X[3]), .B(xor_1_out[3]), .Cin(fa_3_cout), .F(F[3]), .Cout(Cout));

  // Other names for the same wires on the sheet: SUM[3:0] = F; 操作数x[3:0] = X; 操作数y[3:0] = Y

  // Notes on the sheet:
  //   输入引脚
  //   +
  //   =
  //   请勿修改引脚名称、电路名称及电路封装外观
  //   提示：使用独立逻辑门及全加器FA子电路实现4位二进制数加减法器，禁止直接使用加减法器组件。
  //   输出引脚
endmodule

module FA (
  input  A,
  input  B,
  input  Cin,
  output F,
  output Cout
);

  wire and_1_out, and_2_out, and_3_out;

  xor xor_1 (F, A, B, Cin);
  and and_1 (and_1_out, A, B);
  and and_2 (and_2_out, B, Cin);
  and and_3 (and_3_out, A, Cin);
  or or_1 (Cout, and_1_out, and_2_out, and_3_out);

  // Notes on the sheet:
  //   全加器
endmodule

module BarrelSFT8b (
  input  [7:0] DataIn,
  input  [2:0] shamt,
  input  IN,
  input  L_R,
  input  A_L,
  output [7:0] DataOut
);

  wire and_1_out, and_3_out, and_4_out, and_6_out, and_7_out, and_8_out, and_10_out;
  wire [7:0] multiplexer_1_out, multiplexer_2_out;
  wire [7:7] and_5_out, and_9_out;

  and and_1 (and_1_out, A_L, DataIn[7]);
  // AND_Gate and_2 has open pins: in0=DataIn[7], in1=A_L, out=open
  Multiplexer #(.select(2), .width(8), .enable("false")) multiplexer_1 (
    .in0(DataIn), .in1(DataIn), .in2({IN, DataIn[7:1]}), .in3({DataIn[6:0], IN}), .out(multiplexer_1_out),
    .sel({shamt[0], L_R}));
  and and_3 (and_3_out, A_L, multiplexer_1_out[6]);
  and and_4 (and_4_out, A_L, multiplexer_1_out[7]);
  and and_5 (and_5_out[7], multiplexer_1_out[7], A_L);
  Multiplexer #(.select(2), .width(8), .enable("false")) multiplexer_2 (
    .in0(multiplexer_1_out), .in1(multiplexer_1_out), .in2({and_5_out[7], IN, multiplexer_1_out[7:2]}),
    .in3({multiplexer_1_out[5:0], {2{IN}}}), .out(multiplexer_2_out), .sel({shamt[1], L_R}));
  and and_6 (and_6_out, A_L, multiplexer_2_out[4]);
  and and_7 (and_7_out, A_L, multiplexer_2_out[5]);
  and and_8 (and_8_out, A_L, multiplexer_2_out[6]);
  and and_9 (and_9_out[7], multiplexer_2_out[7], A_L);
  and and_10 (and_10_out, A_L, multiplexer_2_out[7]);
  Multiplexer #(.select(2), .width(8), .enable("false")) multiplexer_3 (
    .in0(multiplexer_2_out), .in1(multiplexer_2_out), .in2({{3{and_9_out[7]}}, IN, multiplexer_2_out[7:4]}),
    .in3({multiplexer_2_out[3:0], {4{IN}}}), .out(DataOut), .sel({shamt[2], L_R}));

  // Other names for the same wires on the sheet: Din[7:0] = DataIn; Input = IN; Left_Right = L_R; Arth_Logic = A_L;
  //   Dout[7:0] = DataOut

  // Notes on the sheet:
  //   L/R,A/L: 00逻辑右移，01算术右移，10逻辑左移，11：循环左移
  //   输入引脚
  //   1
  //   请勿修改引脚名称、电路名称及电路封装外观
  //   提示：使用多路选择器级联实现8位桶形移位器，禁止直接使用移位器组件。
  //   对选择器，00/01都不移动；10右移，11左移
  //   输出引脚
  //   2
  //   4
endmodule

module CRA (
  input  [7:0] X,
  input  [7:0] Y,
  output [15:0] Prod
);

  wire cra_cell_2_a_3, cra_cell_2_cout, cra_cell_2_m, cra_cell_3_b_3, cra_cell_3_cout, cra_cell_4_p1,
       cra_cell_4_p2, cra_cell_4_p3, cra_cell_4_p4, cra_cell_4_p5, cra_cell_4_p6, cra_cell_4_p8,
       cra_cell_4_p9, cra_cell_5_a_3, cra_cell_5_b_3, cra_cell_5_cout, cra_cell_5_m, cra_cell_6_b_3,
       cra_cell_6_cout, cra_cell_7_m, cra_cell_8_a_3, cra_cell_8_m, cra_cell_9_a_3, cra_cell_9_b_3,
       cra_cell_9_cout, cra_cell_9_m, cra_cell_10_p1, cra_cell_10_p2, cra_cell_10_p3, cra_cell_10_p5,
       cra_cell_10_p6, cra_cell_10_p10, cra_cell_10_p11, cra_cell_11_a_3, cra_cell_11_cout, cra_cell_11_m,
       cra_cell_12_a_3, cra_cell_12_b_3, cra_cell_12_cout, cra_cell_12_m, cra_cell_13_a_3, cra_cell_13_b_3,
       cra_cell_13_cout, cra_cell_13_m, cra_cell_14_b_3, cra_cell_14_cout, cra_cell_14_m, cra_cell_16_a_3,
       cra_cell_16_cout, cra_cell_16_m, cra_cell_17_a_3, cra_cell_17_b_3, cra_cell_17_cout, cra_cell_17_m,
       cra_cell_18_b_3, cra_cell_18_cout, cra_cell_18_m, cra_cell_19_a_3, cra_cell_19_b_3, cra_cell_19_cout,
       cra_cell_19_m, cra_cell_20_a_3, cra_cell_20_b_3, cra_cell_20_cout, cra_cell_20_m, cra_cell_21_b_3,
       cra_cell_21_cout, cra_cell_22_a_3, cra_cell_22_cout, cra_cell_22_m, cra_cell_23_a_3, cra_cell_23_b_3,
       cra_cell_23_cout, cra_cell_23_m, cra_cell_24_a_3, cra_cell_24_b_3, cra_cell_24_cout, cra_cell_24_m,
       cra_cell_25_a_3, cra_cell_25_b_3, cra_cell_25_cout, cra_cell_25_m, cra_cell_26_a_3, cra_cell_26_b_3,
       cra_cell_26_cout, cra_cell_26_m, cra_cell_27_a_3, cra_cell_27_b_3, cra_cell_27_cout, cra_cell_27_m,
       cra_cell_28_b_3, cra_cell_28_cout, cra_cell_29_a_3, cra_cell_29_cout, cra_cell_29_m, cra_cell_30_a_3,
       cra_cell_30_b_3, cra_cell_30_cout, cra_cell_30_m, cra_cell_31_a_3, cra_cell_31_b_3, cra_cell_31_cout,
       cra_cell_31_m, cra_cell_32_a_3, cra_cell_32_b_3, cra_cell_32_cout, cra_cell_32_m, cra_cell_33_a_3,
       cra_cell_33_b_3, cra_cell_33_cout, cra_cell_33_m, cra_cell_34_a_3, cra_cell_34_b_3, cra_cell_34_cout,
       cra_cell_34_m, cra_cell_35_a_3, cra_cell_35_b_3, cra_cell_35_cout, cra_cell_35_m, cra_cell_36_b_3,
       cra_cell_36_cout, cra_cell_37_a_3, cra_cell_37_b_3, cra_cell_37_cout, cra_cell_37_m, cra_cell_38_a_3,
       cra_cell_38_b_3, cra_cell_38_cout, cra_cell_38_m, cra_cell_39_a_3, cra_cell_39_b_3, cra_cell_39_cout,
       cra_cell_39_m, cra_cell_40_a_3, cra_cell_40_b_3, cra_cell_40_cout, cra_cell_40_m, cra_cell_41_b_3,
       cra_cell_41_cout, cra_cell_41_m, cra_cell_42_a_3, cra_cell_42_b_3, cra_cell_42_cout, cra_cell_42_m,
       cra_cell_43_a_3, cra_cell_43_b_3, cra_cell_43_cout, cra_cell_44_a_3, cra_cell_44_b_3,
       cra_cell_44_cout, cra_cell_44_m, cra_cell_45_a_3, cra_cell_45_b_3, cra_cell_45_cout, cra_cell_45_m,
       cra_cell_46_a_3, cra_cell_46_b_3, cra_cell_46_cout, cra_cell_46_m, cra_cell_47_a_3, cra_cell_47_b_3,
       cra_cell_47_cout, cra_cell_47_m, cra_cell_48_b_3, cra_cell_48_cout, cra_cell_48_m, cra_cell_49_a_3,
       cra_cell_49_b_3, cra_cell_49_cout, cra_cell_50_a_3, cra_cell_50_b_3, cra_cell_50_cout, cra_cell_50_m,
       cra_cell_51_a_3, cra_cell_51_b_3, cra_cell_51_cout, cra_cell_51_m, cra_cell_52_a_3, cra_cell_52_b_3,
       cra_cell_52_cout, cra_cell_52_m, cra_cell_53_a_3, cra_cell_53_b_3, cra_cell_53_cout, cra_cell_53_m,
       cra_cell_54_a_3, cra_cell_54_b_3, cra_cell_54_cout, cra_cell_55_a_3, cra_cell_55_b_3,
       cra_cell_55_cout, cra_cell_55_m, cra_cell_56_a_3, cra_cell_56_b_3, cra_cell_56_cout, cra_cell_56_m,
       cra_cell_57_a_3, cra_cell_57_b_3, cra_cell_57_cout, cra_cell_57_m, cra_cell_58_a_3, cra_cell_58_b_3,
       cra_cell_58_cout, cra_cell_59_a_3, cra_cell_59_b_3, cra_cell_59_cout, cra_cell_59_m, cra_cell_60_a_3,
       cra_cell_60_b_3, cra_cell_60_cout, cra_cell_60_m, cra_cell_61_a_3, cra_cell_61_b_3, cra_cell_61_cout,
       cra_cell_62_a_3, cra_cell_62_b_3, cra_cell_62_cout, cra_cell_62_m, cra_cell_63_a_3, cra_cell_63_b_3,
       cra_cell_63_cout, cra_cell_64_a_3, cra_cell_64_b_3, cra_cell_64_cout;

  CRA_cell cra_cell_1 (
    .M(Prod[14]), .Cout(Prod[15]), .A_2(cra_cell_2_cout), .B_2(cra_cell_3_cout), .A(cra_cell_2_a_3),
    .B(cra_cell_3_b_3));  // open: B_3, A_3
  CRA_cell cra_cell_2 (
    .A_3(cra_cell_2_a_3), .M(cra_cell_2_m), .Cout(cra_cell_2_cout), .A_2(cra_cell_4_p1),
    .B_2(cra_cell_5_cout), .A(cra_cell_4_p3), .B(cra_cell_5_b_3));  // open: B_3
  CRA_cell cra_cell_3 (
    .B_3(cra_cell_3_b_3), .M(Prod[13]), .Cout(cra_cell_3_cout), .A_2(cra_cell_2_m), .B_2(cra_cell_6_cout),
    .A(cra_cell_5_a_3), .B(cra_cell_6_b_3));  // open: A_3
  // CRA_cell cra_cell_4: pin names not known; wires that end beside it: cra_cell_4_p1, cra_cell_4_p2, cra_cell_4_p3, cra_cell_4_p4, cra_cell_4_p5, cra_cell_4_p6, cra_cell_4_p6, cra_cell_4_p8, cra_cell_4_p9
  CRA_cell cra_cell_5 (
    .B_3(cra_cell_5_b_3), .A_3(cra_cell_5_a_3), .M(cra_cell_5_m), .Cout(cra_cell_5_cout),
    .A_2(cra_cell_4_p5), .B_2(cra_cell_9_cout), .A(cra_cell_8_a_3), .B(cra_cell_9_b_3));
  CRA_cell cra_cell_6 (
    .B_3(cra_cell_6_b_3), .M(Prod[12]), .Cout(cra_cell_6_cout), .A_2(cra_cell_5_m), .B_2(cra_cell_10_p2),
    .A(cra_cell_9_a_3), .B(cra_cell_10_p1));  // open: A_3
  CRA_cell cra_cell_7 (
    .A_3(cra_cell_4_p2), .M(cra_cell_7_m), .Cout(cra_cell_4_p4), .A_2(cra_cell_11_cout),
    .B_2(cra_cell_12_cout), .A(cra_cell_11_a_3), .B(cra_cell_12_b_3));  // open: B_3
  CRA_cell cra_cell_8 (
    .B_3(cra_cell_4_p8), .A_3(cra_cell_8_a_3), .M(cra_cell_8_m), .Cout(cra_cell_4_p9), .A_2(cra_cell_7_m),
    .B_2(cra_cell_13_cout), .A(cra_cell_12_a_3), .B(cra_cell_13_b_3));
  CRA_cell cra_cell_9 (
    .B_3(cra_cell_9_b_3), .A_3(cra_cell_9_a_3), .M(cra_cell_9_m), .Cout(cra_cell_9_cout), .A_2(cra_cell_8_m),
    .B_2(cra_cell_14_cout), .A(cra_cell_13_a_3), .B(cra_cell_14_b_3));
  // CRA_cell cra_cell_10: pin names not known; wires that end beside it: cra_cell_10_p1, cra_cell_10_p2, cra_cell_10_p3, cra_cell_10_p3, cra_cell_10_p5, cra_cell_10_p6, cra_cell_10_p6, cra_cell_9_m, Prod[11], cra_cell_10_p10, cra_cell_10_p11
  CRA_cell cra_cell_11 (
    .A_3(cra_cell_11_a_3), .M(cra_cell_11_m), .Cout(cra_cell_11_cout), .A_2(cra_cell_16_cout),
    .B_2(cra_cell_17_cout), .A(cra_cell_16_a_3), .B(cra_cell_17_b_3));  // open: B_3
  CRA_cell cra_cell_12 (
    .B_3(cra_cell_12_b_3), .A_3(cra_cell_12_a_3), .M(cra_cell_12_m), .Cout(cra_cell_12_cout),
    .A_2(cra_cell_11_m), .B_2(cra_cell_18_cout), .A(cra_cell_17_a_3), .B(cra_cell_18_b_3));
  Hex_Digit_Display hex_digit_display_1 (.value(X[7:4]));  // open: dp
  Hex_Digit_Display hex_digit_display_2 (.value(X[3:0]));  // open: dp
  CRA_cell cra_cell_13 (
    .B_3(cra_cell_13_b_3), .A_3(cra_cell_13_a_3), .M(cra_cell_13_m), .Cout(cra_cell_13_cout),
    .A_2(cra_cell_12_m), .B_2(cra_cell_19_cout), .A(cra_cell_13_b_3), .B(cra_cell_19_b_3));
  CRA_cell cra_cell_14 (
    .B_3(cra_cell_14_b_3), .A_3(cra_cell_10_p5), .M(cra_cell_14_m), .Cout(cra_cell_14_cout),
    .A_2(cra_cell_13_m), .B_2(cra_cell_20_cout), .A(cra_cell_19_a_3), .B(cra_cell_20_b_3));
  CRA_cell cra_cell_15 (
    .B_3(cra_cell_10_p10), .M(Prod[10]), .Cout(cra_cell_10_p11), .A_2(cra_cell_14_m), .B_2(cra_cell_21_cout),
    .A(cra_cell_20_a_3), .B(cra_cell_21_b_3));  // open: A_3
  Hex_Digit_Display hex_digit_display_3 (.value(Y[7:4]));  // open: dp
  CRA_cell cra_cell_16 (
    .A_3(cra_cell_16_a_3), .M(cra_cell_16_m), .Cout(cra_cell_16_cout), .A_2(cra_cell_22_cout),
    .B_2(cra_cell_23_cout), .A(cra_cell_22_a_3), .B(cra_cell_23_b_3));  // open: B_3
  CRA_cell cra_cell_17 (
    .B_3(cra_cell_17_b_3), .A_3(cra_cell_17_a_3), .M(cra_cell_17_m), .Cout(cra_cell_17_cout),
    .A_2(cra_cell_16_m), .B_2(cra_cell_24_cout), .A(cra_cell_23_a_3), .B(cra_cell_24_b_3));
  CRA_cell cra_cell_18 (
    .B_3(cra_cell_18_b_3), .A_3(cra_cell_13_b_3), .M(cra_cell_18_m), .Cout(cra_cell_18_cout),
    .A_2(cra_cell_17_m), .B_2(cra_cell_25_cout), .A(cra_cell_24_a_3), .B(cra_cell_25_b_3));
  CRA_cell cra_cell_19 (
    .B_3(cra_cell_19_b_3), .A_3(cra_cell_19_a_3), .M(cra_cell_19_m), .Cout(cra_cell_19_cout),
    .A_2(cra_cell_18_m), .B_2(cra_cell_26_cout), .A(cra_cell_25_a_3), .B(cra_cell_26_b_3));
  CRA_cell cra_cell_20 (
    .B_3(cra_cell_20_b_3), .A_3(cra_cell_20_a_3), .M(cra_cell_20_m), .Cout(cra_cell_20_cout),
    .A_2(cra_cell_19_m), .B_2(cra_cell_27_cout), .A(cra_cell_26_a_3), .B(cra_cell_27_b_3));
  CRA_cell cra_cell_21 (
    .B_3(cra_cell_21_b_3), .M(Prod[9]), .Cout(cra_cell_21_cout), .A_2(cra_cell_20_m), .B_2(cra_cell_28_cout),
    .A(cra_cell_27_a_3), .B(cra_cell_28_b_3));  // open: A_3
  Hex_Digit_Display hex_digit_display_4 (.value(Y[3:0]));  // open: dp
  CRA_cell cra_cell_22 (
    .A_3(cra_cell_22_a_3), .M(cra_cell_22_m), .Cout(cra_cell_22_cout), .A_2(cra_cell_29_cout),
    .B_2(cra_cell_30_cout), .A(cra_cell_29_a_3), .B(cra_cell_30_b_3));  // open: B_3
  CRA_cell cra_cell_23 (
    .B_3(cra_cell_23_b_3), .A_3(cra_cell_23_a_3), .M(cra_cell_23_m), .Cout(cra_cell_23_cout),
    .A_2(cra_cell_22_m), .B_2(cra_cell_31_cout), .A(cra_cell_30_a_3), .B(cra_cell_31_b_3));
  CRA_cell cra_cell_24 (
    .B_3(cra_cell_24_b_3), .A_3(cra_cell_24_a_3), .M(cra_cell_24_m), .Cout(cra_cell_24_cout),
    .A_2(cra_cell_23_m), .B_2(cra_cell_32_cout), .A(cra_cell_31_a_3), .B(cra_cell_32_b_3));
  CRA_cell cra_cell_25 (
    .B_3(cra_cell_25_b_3), .A_3(cra_cell_25_a_3), .M(cra_cell_25_m), .Cout(cra_cell_25_cout),
    .A_2(cra_cell_24_m), .B_2(cra_cell_33_cout), .A(cra_cell_32_a_3), .B(cra_cell_33_b_3));
  Hex_Digit_Display hex_digit_display_5 (.value(Prod[15:12]));  // open: dp
  Hex_Digit_Display hex_digit_display_6 (.value(Prod[11:8]));  // open: dp
  CRA_cell cra_cell_26 (
    .B_3(cra_cell_26_b_3), .A_3(cra_cell_26_a_3), .M(cra_cell_26_m), .Cout(cra_cell_26_cout),
    .A_2(cra_cell_25_m), .B_2(cra_cell_34_cout), .A(cra_cell_33_a_3), .B(cra_cell_34_b_3));
  CRA_cell cra_cell_27 (
    .B_3(cra_cell_27_b_3), .A_3(cra_cell_27_a_3), .M(cra_cell_27_m), .Cout(cra_cell_27_cout),
    .A_2(cra_cell_26_m), .B_2(cra_cell_35_cout), .A(cra_cell_34_a_3), .B(cra_cell_35_b_3));
  CRA_cell cra_cell_28 (
    .B_3(cra_cell_28_b_3), .M(Prod[8]), .Cout(cra_cell_28_cout), .A_2(cra_cell_27_m), .B_2(cra_cell_36_cout),
    .A(cra_cell_35_a_3), .B(cra_cell_36_b_3));  // open: A_3
  Hex_Digit_Display hex_digit_display_7 (.value(Prod[7:4]));  // open: dp
  Hex_Digit_Display hex_digit_display_8 (.value(Prod[3:0]));  // open: dp
  CRA_cell cra_cell_29 (
    .A_3(cra_cell_29_a_3), .M(cra_cell_29_m), .Cout(cra_cell_29_cout), .A_2(1'b0), .B_2(cra_cell_37_cout),
    .A(X[7]), .B(cra_cell_37_b_3));  // open: B_3
  CRA_cell cra_cell_30 (
    .B_3(cra_cell_30_b_3), .A_3(cra_cell_30_a_3), .M(cra_cell_30_m), .Cout(cra_cell_30_cout),
    .A_2(cra_cell_29_m), .B_2(cra_cell_38_cout), .A(cra_cell_37_a_3), .B(cra_cell_38_b_3));
  CRA_cell cra_cell_31 (
    .B_3(cra_cell_31_b_3), .A_3(cra_cell_31_a_3), .M(cra_cell_31_m), .Cout(cra_cell_31_cout),
    .A_2(cra_cell_30_m), .B_2(cra_cell_39_cout), .A(cra_cell_38_a_3), .B(cra_cell_39_b_3));
  CRA_cell cra_cell_32 (
    .B_3(cra_cell_32_b_3), .A_3(cra_cell_32_a_3), .M(cra_cell_32_m), .Cout(cra_cell_32_cout),
    .A_2(cra_cell_31_m), .B_2(cra_cell_40_cout), .A(cra_cell_39_a_3), .B(cra_cell_40_b_3));
  CRA_cell cra_cell_33 (
    .B_3(cra_cell_33_b_3), .A_3(cra_cell_33_a_3), .M(cra_cell_33_m), .Cout(cra_cell_33_cout),
    .A_2(cra_cell_32_m), .B_2(cra_cell_41_cout), .A(cra_cell_40_a_3), .B(cra_cell_41_b_3));
  CRA_cell cra_cell_34 (
    .B_3(cra_cell_34_b_3), .A_3(cra_cell_34_a_3), .M(cra_cell_34_m), .Cout(cra_cell_34_cout),
    .A_2(cra_cell_33_m), .B_2(cra_cell_42_cout), .A(cra_cell_34_b_3), .B(cra_cell_42_b_3));
  CRA_cell cra_cell_35 (
    .B_3(cra_cell_35_b_3), .A_3(cra_cell_35_a_3), .M(cra_cell_35_m), .Cout(cra_cell_35_cout),
    .A_2(cra_cell_34_m), .B_2(cra_cell_43_cout), .A(cra_cell_42_a_3), .B(cra_cell_43_b_3));
  CRA_cell cra_cell_36 (
    .B_3(cra_cell_36_b_3), .M(Prod[7]), .Cout(cra_cell_36_cout), .A_2(cra_cell_35_m), .B_2(1'b0),
    .A(cra_cell_43_a_3), .B(Y[7]));  // open: A_3
  CRA_cell cra_cell_37 (
    .B_3(cra_cell_37_b_3), .A_3(cra_cell_37_a_3), .M(cra_cell_37_m), .Cout(cra_cell_37_cout), .A_2(1'b0),
    .B_2(cra_cell_44_cout), .A(X[6]), .B(cra_cell_44_b_3));
  CRA_cell cra_cell_38 (
    .B_3(cra_cell_38_b_3), .A_3(cra_cell_38_a_3), .M(cra_cell_38_m), .Cout(cra_cell_38_cout),
    .A_2(cra_cell_37_m), .B_2(cra_cell_45_cout), .A(cra_cell_44_a_3), .B(cra_cell_45_b_3));
  CRA_cell cra_cell_39 (
    .B_3(cra_cell_39_b_3), .A_3(cra_cell_39_a_3), .M(cra_cell_39_m), .Cout(cra_cell_39_cout),
    .A_2(cra_cell_38_m), .B_2(cra_cell_46_cout), .A(cra_cell_45_a_3), .B(cra_cell_46_b_3));
  CRA_cell cra_cell_40 (
    .B_3(cra_cell_40_b_3), .A_3(cra_cell_40_a_3), .M(cra_cell_40_m), .Cout(cra_cell_40_cout),
    .A_2(cra_cell_39_m), .B_2(cra_cell_47_cout), .A(cra_cell_46_a_3), .B(cra_cell_47_b_3));
  CRA_cell cra_cell_41 (
    .B_3(cra_cell_41_b_3), .A_3(cra_cell_34_b_3), .M(cra_cell_41_m), .Cout(cra_cell_41_cout),
    .A_2(cra_cell_40_m), .B_2(cra_cell_48_cout), .A(cra_cell_47_a_3), .B(cra_cell_48_b_3));
  CRA_cell cra_cell_42 (
    .B_3(cra_cell_42_b_3), .A_3(cra_cell_42_a_3), .M(cra_cell_42_m), .Cout(cra_cell_42_cout),
    .A_2(cra_cell_41_m), .B_2(cra_cell_49_cout), .A(cra_cell_42_b_3), .B(cra_cell_49_b_3));
  CRA_cell cra_cell_43 (
    .B_3(cra_cell_43_b_3), .A_3(cra_cell_43_a_3), .M(Prod[6]), .Cout(cra_cell_43_cout), .A_2(cra_cell_42_m),
    .B_2(1'b0), .A(cra_cell_49_a_3), .B(Y[6]));
  CRA_cell cra_cell_44 (
    .B_3(cra_cell_44_b_3), .A_3(cra_cell_44_a_3), .M(cra_cell_44_m), .Cout(cra_cell_44_cout), .A_2(1'b0),
    .B_2(cra_cell_50_cout), .A(X[5]), .B(cra_cell_50_b_3));
  CRA_cell cra_cell_45 (
    .B_3(cra_cell_45_b_3), .A_3(cra_cell_45_a_3), .M(cra_cell_45_m), .Cout(cra_cell_45_cout),
    .A_2(cra_cell_44_m), .B_2(cra_cell_51_cout), .A(cra_cell_50_a_3), .B(cra_cell_51_b_3));
  CRA_cell cra_cell_46 (
    .B_3(cra_cell_46_b_3), .A_3(cra_cell_46_a_3), .M(cra_cell_46_m), .Cout(cra_cell_46_cout),
    .A_2(cra_cell_45_m), .B_2(cra_cell_52_cout), .A(cra_cell_51_a_3), .B(cra_cell_52_b_3));
  CRA_cell cra_cell_47 (
    .B_3(cra_cell_47_b_3), .A_3(cra_cell_47_a_3), .M(cra_cell_47_m), .Cout(cra_cell_47_cout),
    .A_2(cra_cell_46_m), .B_2(cra_cell_53_cout), .A(cra_cell_52_a_3), .B(cra_cell_53_b_3));
  CRA_cell cra_cell_48 (
    .B_3(cra_cell_48_b_3), .A_3(cra_cell_42_b_3), .M(cra_cell_48_m), .Cout(cra_cell_48_cout),
    .A_2(cra_cell_47_m), .B_2(cra_cell_54_cout), .A(cra_cell_53_a_3), .B(cra_cell_54_b_3));
  CRA_cell cra_cell_49 (
    .B_3(cra_cell_49_b_3), .A_3(cra_cell_49_a_3), .M(Prod[5]), .Cout(cra_cell_49_cout), .A_2(cra_cell_48_m),
    .B_2(1'b0), .A(cra_cell_54_a_3), .B(Y[5]));
  CRA_cell cra_cell_50 (
    .B_3(cra_cell_50_b_3), .A_3(cra_cell_50_a_3), .M(cra_cell_50_m), .Cout(cra_cell_50_cout), .A_2(1'b0),
    .B_2(cra_cell_55_cout), .A(X[4]), .B(cra_cell_55_b_3));
  CRA_cell cra_cell_51 (
    .B_3(cra_cell_51_b_3), .A_3(cra_cell_51_a_3), .M(cra_cell_51_m), .Cout(cra_cell_51_cout),
    .A_2(cra_cell_50_m), .B_2(cra_cell_56_cout), .A(cra_cell_55_a_3), .B(cra_cell_56_b_3));
  CRA_cell cra_cell_52 (
    .B_3(cra_cell_52_b_3), .A_3(cra_cell_52_a_3), .M(cra_cell_52_m), .Cout(cra_cell_52_cout),
    .A_2(cra_cell_51_m), .B_2(cra_cell_57_cout), .A(cra_cell_56_a_3), .B(cra_cell_57_b_3));
  CRA_cell cra_cell_53 (
    .B_3(cra_cell_53_b_3), .A_3(cra_cell_53_a_3), .M(cra_cell_53_m), .Cout(cra_cell_53_cout),
    .A_2(cra_cell_52_m), .B_2(cra_cell_58_cout), .A(cra_cell_57_a_3), .B(cra_cell_58_b_3));
  CRA_cell cra_cell_54 (
    .B_3(cra_cell_54_b_3), .A_3(cra_cell_54_a_3), .M(Prod[4]), .Cout(cra_cell_54_cout), .A_2(cra_cell_53_m),
    .B_2(1'b0), .A(cra_cell_58_a_3), .B(Y[4]));
  CRA_cell cra_cell_55 (
    .B_3(cra_cell_55_b_3), .A_3(cra_cell_55_a_3), .M(cra_cell_55_m), .Cout(cra_cell_55_cout), .A_2(1'b0),
    .B_2(cra_cell_59_cout), .A(X[3]), .B(cra_cell_59_b_3));
  CRA_cell cra_cell_56 (
    .B_3(cra_cell_56_b_3), .A_3(cra_cell_56_a_3), .M(cra_cell_56_m), .Cout(cra_cell_56_cout),
    .A_2(cra_cell_55_m), .B_2(cra_cell_60_cout), .A(cra_cell_59_a_3), .B(cra_cell_60_b_3));
  CRA_cell cra_cell_57 (
    .B_3(cra_cell_57_b_3), .A_3(cra_cell_57_a_3), .M(cra_cell_57_m), .Cout(cra_cell_57_cout),
    .A_2(cra_cell_56_m), .B_2(cra_cell_61_cout), .A(cra_cell_60_a_3), .B(cra_cell_61_b_3));
  CRA_cell cra_cell_58 (
    .B_3(cra_cell_58_b_3), .A_3(cra_cell_58_a_3), .M(Prod[3]), .Cout(cra_cell_58_cout), .A_2(cra_cell_57_m),
    .B_2(1'b0), .A(cra_cell_61_a_3), .B(Y[3]));
  CRA_cell cra_cell_59 (
    .B_3(cra_cell_59_b_3), .A_3(cra_cell_59_a_3), .M(cra_cell_59_m), .Cout(cra_cell_59_cout), .A_2(1'b0),
    .B_2(cra_cell_62_cout), .A(X[2]), .B(cra_cell_62_b_3));
  CRA_cell cra_cell_60 (
    .B_3(cra_cell_60_b_3), .A_3(cra_cell_60_a_3), .M(cra_cell_60_m), .Cout(cra_cell_60_cout),
    .A_2(cra_cell_59_m), .B_2(cra_cell_63_cout), .A(cra_cell_62_a_3), .B(cra_cell_63_b_3));
  CRA_cell cra_cell_61 (
    .B_3(cra_cell_61_b_3), .A_3(cra_cell_61_a_3), .M(Prod[2]), .Cout(cra_cell_61_cout), .A_2(cra_cell_60_m),
    .B_2(1'b0), .A(cra_cell_63_a_3), .B(Y[2]));
  CRA_cell cra_cell_62 (
    .B_3(cra_cell_62_b_3), .A_3(cra_cell_62_a_3), .M(cra_cell_62_m), .Cout(cra_cell_62_cout), .A_2(1'b0),
    .B_2(cra_cell_64_cout), .A(X[1]), .B(cra_cell_64_b_3));
  CRA_cell cra_cell_63 (
    .B_3(cra_cell_63_b_3), .A_3(cra_cell_63_a_3), .M(Prod[1]), .Cout(cra_cell_63_cout), .A_2(cra_cell_62_m),
    .B_2(1'b0), .A(cra_cell_64_a_3), .B(Y[1]));
  CRA_cell cra_cell_64 (
    .B_3(cra_cell_64_b_3), .A_3(cra_cell_64_a_3), .M(Prod[0]), .Cout(cra_cell_64_cout), .A_2(1'b0),
    .B_2(1'b0), .A(X[0]), .B(Y[0]));

  // Other names for the same wires on the sheet: Z[15:0] = Prod

  // Notes on the sheet:
  //   输入引脚
  //   请勿修改引脚名称、电路名称及电路封装外观
  //   提示: 采用无符号数一位乘法实现4位二进制乘法器，禁止直接使用乘法器组件
  //   输出引脚
  //   X
  //   =
endmodule

module CRA_cell (
  input  A,
  input  A_2,
  input  B,
  input  B_2,
  output A_3,
  output M,
  output B_3,
  output Cout
);

  wire and_1_out;

  and and_1 (and_1_out, B, A);
  FA fa_1 (.A(and_1_out), .B(A_2), .Cin(B_2), .F(M), .Cout(Cout));

  assign A_3 = A;
  assign B_3 = B;

  // Other names for the same wires on the sheet: A1 = A; B1 = B; Cin = B_2; Mult = A_2
endmodule
