// Logisim project lab3.4.circ as structural Verilog: 2 circuits, main circuit main
module main (
  input  [4:0] R1_num,
  input  [4:0] R2_num,
  input  [4:0] Write_Reg_num,
  input  [31:0] Din,
  input  Write_Enable,
  input  Clock,
  output [31:0] Reg1Out,
  output [31:0] Reg2Out
);

  wire and_1_out, and_2_out, and_3_out, and_4_out, and_5_out, and_6_out, and_7_out, and_8_out, and_9_out,
       and_10_out, and_11_out, and_12_out, and_13_out, and_14_out, and_15_out, and_16_out, and_17_out,
       and_18_out, and_19_out, and_20_out, and_21_out, and_22_out, and_23_out, and_24_out, and_25_out,
       and_26_out, and_27_out, and_28_out, and_29_out, and_30_out, and_31_out, and_32_out, decoder_1_out0,
       decoder_1_out1, decoder_1_out2, decoder_1_out3, decoder_1_out4, decoder_1_out5, decoder_1_out6,
       decoder_1_out7, decoder_1_out8, decoder_1_out9, decoder_1_out10, decoder_1_out11, decoder_1_out12,
       decoder_1_out13, decoder_1_out14, decoder_1_out15, decoder_1_out16, decoder_1_out17, decoder_1_out18,
       decoder_1_out19, decoder_1_out20, decoder_1_out21, decoder_1_out22, decoder_1_out23, decoder_1_out24,
       decoder_1_out25, decoder_1_out26, decoder_1_out27, decoder_1_out28, decoder_1_out29, decoder_1_out30,
       decoder_1_out31, undriven;
  wire [31:0] _0_q, _1_q, _2_q, _3_q, _4_q, _5_q, _6_q, _7_q, _8_q, _9_q, register_1_q, register_2_q,
       register_3_q, register_4_q, register_5_q, register_6_q, register_7_q, register_8_q, register_9_q,
       register_10_q, register_11_q, register_12_q, register_13_q, register_14_q, register_15_q,
       register_16_q, register_17_q, register_18_q, register_19_q, register_20_q, register_21_q,
       register_22_q;

  Decoder #(.select(5), .enable("false")) decoder_1 (
    .out0(decoder_1_out0), .out1(decoder_1_out1), .out2(decoder_1_out2), .out3(decoder_1_out3),
    .out4(decoder_1_out4), .out5(decoder_1_out5), .out6(decoder_1_out6), .out7(decoder_1_out7),
    .out8(decoder_1_out8), .out9(decoder_1_out9), .out10(decoder_1_out10), .out11(decoder_1_out11),
    .out12(decoder_1_out12), .out13(decoder_1_out13), .out14(decoder_1_out14), .out15(decoder_1_out15),
    .out16(decoder_1_out16), .out17(decoder_1_out17), .out18(decoder_1_out18), .out19(decoder_1_out19),
    .out20(decoder_1_out20), .out21(decoder_1_out21), .out22(decoder_1_out22), .out23(decoder_1_out23),
    .out24(decoder_1_out24), .out25(decoder_1_out25), .out26(decoder_1_out26), .out27(decoder_1_out27),
    .out28(decoder_1_out28), .out29(decoder_1_out29), .out30(decoder_1_out30), .out31(decoder_1_out31),
    .sel(Write_Reg_num));
  and and_1 (and_1_out, Write_Enable, decoder_1_out0);
  and and_2 (and_2_out, decoder_1_out1, Write_Enable);
  and and_3 (and_3_out, Write_Enable, decoder_1_out2);
  and and_4 (and_4_out, decoder_1_out3, Write_Enable);
  and and_5 (and_5_out, decoder_1_out4, Write_Enable);
  and and_6 (and_6_out, Write_Enable, decoder_1_out5);
  and and_7 (and_7_out, decoder_1_out6, Write_Enable);
  and and_8 (and_8_out, decoder_1_out7, Write_Enable);
  and and_9 (and_9_out, Write_Enable, decoder_1_out8);
  and and_10 (and_10_out, Write_Enable, decoder_1_out9);
  and and_11 (and_11_out, Write_Enable, decoder_1_out10);
  and and_12 (and_12_out, Write_Enable, decoder_1_out11);
  and and_13 (and_13_out, decoder_1_out12, Write_Enable);
  and and_14 (and_14_out, decoder_1_out13, Write_Enable);
  and and_15 (and_15_out, decoder_1_out14, Write_Enable);
  and and_16 (and_16_out, decoder_1_out15, Write_Enable);
  and and_17 (and_17_out, Write_Enable, decoder_1_out16);
  and and_18 (and_18_out, Write_Enable, decoder_1_out17);
  and and_19 (and_19_out, decoder_1_out18, Write_Enable);
  and and_20 (and_20_out, Write_Enable, decoder_1_out19);
  and and_21 (and_21_out, decoder_1_out20, Write_Enable);
  and and_22 (and_22_out, decoder_1_out21, Write_Enable);
  and and_23 (and_23_out, decoder_1_out22, Write_Enable);
  and and_24 (and_24_out, decoder_1_out23, Write_Enable);
  and and_25 (and_25_out, decoder_1_out24, Write_Enable);
  and and_26 (and_26_out, Write_Enable, decoder_1_out25);
  and and_27 (and_27_out, decoder_1_out26, Write_Enable);
  and and_28 (and_28_out, decoder_1_out27, Write_Enable);
  and and_29 (and_29_out, Write_Enable, decoder_1_out28);
  and and_30 (and_30_out, decoder_1_out29, Write_Enable);
  and and_31 (and_31_out, Write_Enable, decoder_1_out30);
  and and_32 (and_32_out, decoder_1_out31, Write_Enable);
  Register #(.width(32), .Select("high")) _0 (
    .D(Din), .en(and_1_out), .Q(_0_q), .clk(Clock), .preset(undriven));  // open: clr, cs
  Register #(.width(32), .Select("high")) _1 (
    .D(Din), .en(and_2_out), .Q(_1_q), .clk(Clock), .clr(1'b0), .cs(1'b1), .preset(1'b0));
  Register #(.width(32), .Select("high")) _2 (
    .D(Din), .en(and_3_out), .Q(_2_q), .clk(Clock), .clr(1'b0), .cs(1'b1), .preset(1'b0));
  Register #(.width(32), .Select("high")) _3 (
    .D(Din), .en(and_4_out), .Q(_3_q), .clk(Clock), .clr(1'b0), .cs(1'b1), .preset(1'b0));
  Register #(.width(32), .Select("high")) _4 (
    .D(Din), .en(and_5_out), .Q(_4_q), .clk(Clock), .clr(1'b0), .cs(1'b1), .preset(1'b0));
  Register #(.width(32), .Select("high")) _5 (
    .D(Din), .en(and_6_out), .Q(_5_q), .clk(Clock), .clr(1'b0), .cs(1'b1), .preset(1'b0));
  Register #(.width(32), .Select("high")) _6 (
    .D(Din), .en(and_7_out), .Q(_6_q), .clk(Clock), .clr(1'b0), .cs(1'b1), .preset(1'b0));
  Register #(.width(32), .Select("high")) _7 (
    .D(Din), .en(and_8_out), .Q(_7_q), .clk(Clock), .clr(1'b0), .cs(1'b1), .preset(1'b0));
  Register #(.width(32), .Select("high")) _8 (
    .D(Din), .en(and_9_out), .Q(_8_q), .clk(Clock), .clr(1'b0), .cs(1'b1), .preset(1'b0));
  Register #(.width(32), .Select("high")) _9 (
    .D(Din), .en(and_10_out), .Q(_9_q), .clk(Clock), .clr(1'b0), .cs(1'b1), .preset(1'b0));
  Register #(.width(32), .Select("high")) register_1 (
    .D(Din), .en(and_11_out), .Q(register_1_q), .clk(Clock), .clr(1'b0), .cs(1'b1), .preset(1'b0));
  Register #(.width(32), .Select("high")) register_2 (
    .D(Din), .en(and_12_out), .Q(register_2_q), .clk(Clock), .clr(1'b0), .cs(1'b1), .preset(1'b0));
  Register #(.width(32), .Select("high")) register_3 (
    .D(Din), .en(and_13_out), .Q(register_3_q), .clk(Clock), .clr(1'b0), .cs(1'b1), .preset(1'b0));
  Register #(.width(32), .Select("high")) register_4 (
    .D(Din), .en(and_14_out), .Q(register_4_q), .clk(Clock), .clr(1'b0), .cs(1'b1), .preset(1'b0));
  Register #(.width(32), .Select("high")) register_5 (
    .D(Din), .en(and_15_out), .Q(register_5_q), .clk(Clock), .clr(1'b0), .cs(1'b1), .preset(1'b0));
  Register #(.width(32), .Select("high")) register_6 (
    .D(Din), .en(and_16_out), .Q(register_6_q), .clk(Clock), .clr(1'b0), .cs(1'b1), .preset(1'b0));
  Register #(.width(32), .Select("high")) register_7 (
    .D(Din), .en(and_17_out), .Q(register_7_q), .clk(Clock), .clr(1'b0), .cs(1'b1), .preset(1'b0));
  Register #(.width(32), .Select("high")) register_8 (
    .D(Din), .en(and_18_out), .Q(register_8_q), .clk(Clock), .clr(1'b0), .cs(1'b1), .preset(1'b0));
  Register #(.width(32), .Select("high")) register_9 (
    .D(Din), .en(and_19_out), .Q(register_9_q), .clk(Clock), .clr(1'b0), .cs(1'b1), .preset(1'b0));
  Register #(.width(32), .Select("high")) register_10 (
    .D(Din), .en(and_20_out), .Q(register_10_q), .clk(Clock), .clr(1'b0), .cs(1'b1), .preset(1'b0));
  Register #(.width(32), .Select("high")) register_11 (
    .D(Din), .en(and_21_out), .Q(register_11_q), .clk(Clock), .clr(1'b0), .cs(1'b1), .preset(1'b0));
  Register #(.width(32), .Select("high")) register_12 (
    .D(Din), .en(and_22_out), .Q(register_12_q), .clk(Clock), .clr(1'b0), .cs(1'b1), .preset(1'b0));
  Register #(.width(32), .Select("high")) register_13 (
    .D(Din), .en(and_23_out), .Q(register_13_q), .clk(Clock), .clr(1'b0), .cs(1'b1), .preset(1'b0));
  Register #(.width(32), .Select("high")) register_14 (
    .D(Din), .en(and_24_out), .Q(register_14_q), .clk(Clock), .clr(1'b0), .cs(1'b1), .preset(1'b0));
  Register #(.width(32), .Select("high")) register_15 (
    .D(Din), .en(and_25_out), .Q(register_15_q), .clk(Clock), .clr(1'b0), .cs(1'b1), .preset(1'b0));
  Register #(.width(32), .Select("high")) register_16 (
    .D(Din), .en(and_26_out), .Q(register_16_q), .clk(Clock), .clr(1'b0), .cs(1'b1), .preset(1'b0));
  Register #(.width(32), .Select("high")) register_17 (
    .D(Din), .en(and_27_out), .Q(register_17_q), .clk(Clock), .clr(1'b0), .cs(1'b1), .preset(1'b0));
  Register #(.width(32), .Select("high")) register_18 (
    .D(Din), .en(and_28_out), .Q(register_18_q), .clk(Clock), .clr(1'b0), .cs(1'b1), .preset(1'b0));
  Register #(.width(32), .Select("high")) register_19 (
    .D(Din), .en(and_29_out), .Q(register_19_q), .clk(Clock), .clr(1'b0), .cs(1'b1), .preset(1'b0));
  Register #(.width(32), .Select("high")) register_20 (
    .D(Din), .en(and_30_out), .Q(register_20_q), .clk(Clock), .clr(1'b0), .cs(1'b1), .preset(1'b0));
  Register #(.width(32), .Select("high")) register_21 (
    .D(Din), .en(and_31_out), .Q(register_21_q), .clk(Clock), .clr(1'b0), .cs(1'b1), .preset(1'b0));
  Register #(.width(32), .Select("high")) register_22 (
    .D(Din), .en(and_32_out), .Q(register_22_q), .clk(Clock), .clr(1'b0), .cs(1'b1), .preset(1'b0));
  Multiplexer #(.select(5), .width(32), .enable("false")) multiplexer_1 (
    .in0(_0_q), .in1(_1_q), .in2(_2_q), .in3(_3_q), .in4(_4_q), .in5(_5_q), .in6(_6_q), .in7(_7_q),
    .in8(_8_q), .in9(_9_q), .in10(register_1_q), .in11(register_2_q), .in12(register_3_q),
    .in13(register_4_q), .in14(register_5_q), .in15(register_6_q), .in16(register_7_q), .in17(register_8_q),
    .in18(register_9_q), .in19(register_10_q), .in20(register_11_q), .in21(register_12_q),
    .in22(register_13_q), .in23(register_14_q), .in24(register_15_q), .in25(register_16_q),
    .in26(register_17_q), .in27(register_18_q), .in28(register_19_q), .in29(register_20_q),
    .in30(register_21_q), .in31(register_22_q), .out(Reg1Out), .sel(R1_num));
  Multiplexer #(.select(5), .width(32), .enable("false")) multiplexer_2 (
    .in0(_0_q), .in1(_1_q), .in2(_2_q), .in3(_3_q), .in4(_4_q), .in5(_5_q), .in6(_6_q), .in7(_7_q),
    .in8(_8_q), .in9(_9_q), .in10(register_1_q), .in11(register_2_q), .in12(register_3_q),
    .in13(register_4_q), .in14(register_5_q), .in15(register_6_q), .in16(register_7_q), .in17(register_8_q),
    .in18(register_9_q), .in19(register_10_q), .in20(register_11_q), .in21(register_12_q),
    .in22(register_13_q), .in23(register_14_q), .in24(register_15_q), .in25(register_16_q),
    .in26(register_17_q), .in27(register_18_q), .in28(register_19_q), .in29(register_20_q),
    .in30(register_21_q), .in31(register_22_q), .out(Reg2Out), .sel(R2_num));

  // Other names for the same wires on the sheet: CLK = Clock; RA[4:0] = R1_num; RB[4:0] = R2_num; RDA[31:0] = Reg1Out;
  //   RDB[31:0] = Reg2Out; RW[4:0] = Write_Reg_num; WE = Write_Enable

  // Notes on the sheet:
  //   输入引脚
  //   请勿修改引脚名称、电路名称及电路封装外观
  //   提示：使用译码器、多路选择器和32位寄存器及逻辑门实现寄存器堆，禁止直接使用存储器组件。
  //   输出引脚
endmodule

module think3 (
  input  [4:0] R1_num,
  input  [4:0] R2_num,
  input  [4:0] Write_Reg_num,
  input  [31:0] Din,
  input  Write_Enable,
  input  Clock,
  output [31:0] Reg1Out,
  output [31:0] Reg2Out
);

  wire and_1_out, and_2_out, and_3_out, and_4_out, and_5_out, and_6_out, and_7_out, and_8_out, and_9_out,
       and_10_out, and_11_out, and_12_out, and_13_out, and_14_out, and_15_out, and_16_out, and_17_out,
       and_18_out, and_19_out, and_20_out, and_21_out, and_22_out, and_23_out, and_24_out, and_25_out,
       and_26_out, and_27_out, and_28_out, and_29_out, and_30_out, and_31_out, and_32_out, decoder_1_out0,
       decoder_1_out1, decoder_1_out2, decoder_1_out3, decoder_1_out4, decoder_1_out5, decoder_1_out6,
       decoder_1_out7, decoder_1_out8, decoder_1_out9, decoder_1_out10, decoder_1_out11, decoder_1_out12,
       decoder_1_out13, decoder_1_out14, decoder_1_out15, decoder_1_out16, decoder_1_out17, decoder_1_out18,
       decoder_1_out19, decoder_1_out20, decoder_1_out21, decoder_1_out22, decoder_1_out23, decoder_1_out24,
       decoder_1_out25, decoder_1_out26, decoder_1_out27, decoder_1_out28, decoder_1_out29, decoder_1_out30,
       decoder_1_out31, undriven;
  wire [31:0] _0_q, _1_q, _2_q, _3_q, _4_q, _5_q, _6_q, _7_q, _8_q, _9_q, register_1_q, register_2_q,
       register_3_q, register_4_q, register_5_q, register_6_q, register_7_q, register_8_q, register_9_q,
       register_10_q, register_11_q, register_12_q, register_13_q, register_14_q, register_15_q,
       register_16_q, register_17_q, register_18_q, register_19_q, register_20_q, register_21_q,
       register_22_q;

  Decoder #(.select(5), .enable("false")) decoder_1 (
    .out0(decoder_1_out0), .out1(decoder_1_out1), .out2(decoder_1_out2), .out3(decoder_1_out3),
    .out4(decoder_1_out4), .out5(decoder_1_out5), .out6(decoder_1_out6), .out7(decoder_1_out7),
    .out8(decoder_1_out8), .out9(decoder_1_out9), .out10(decoder_1_out10), .out11(decoder_1_out11),
    .out12(decoder_1_out12), .out13(decoder_1_out13), .out14(decoder_1_out14), .out15(decoder_1_out15),
    .out16(decoder_1_out16), .out17(decoder_1_out17), .out18(decoder_1_out18), .out19(decoder_1_out19),
    .out20(decoder_1_out20), .out21(decoder_1_out21), .out22(decoder_1_out22), .out23(decoder_1_out23),
    .out24(decoder_1_out24), .out25(decoder_1_out25), .out26(decoder_1_out26), .out27(decoder_1_out27),
    .out28(decoder_1_out28), .out29(decoder_1_out29), .out30(decoder_1_out30), .out31(decoder_1_out31),
    .sel(Write_Reg_num));
  and and_1 (and_1_out, Write_Enable, decoder_1_out0);
  and and_2 (and_2_out, decoder_1_out1, Write_Enable);
  and and_3 (and_3_out, Write_Enable, decoder_1_out2);
  and and_4 (and_4_out, decoder_1_out3, Write_Enable);
  and and_5 (and_5_out, decoder_1_out4, Write_Enable);
  and and_6 (and_6_out, Write_Enable, decoder_1_out5);
  and and_7 (and_7_out, decoder_1_out6, Write_Enable);
  and and_8 (and_8_out, decoder_1_out7, Write_Enable);
  and and_9 (and_9_out, Write_Enable, decoder_1_out8);
  and and_10 (and_10_out, Write_Enable, decoder_1_out9);
  and and_11 (and_11_out, Write_Enable, decoder_1_out10);
  and and_12 (and_12_out, Write_Enable, decoder_1_out11);
  and and_13 (and_13_out, decoder_1_out12, Write_Enable);
  and and_14 (and_14_out, decoder_1_out13, Write_Enable);
  and and_15 (and_15_out, decoder_1_out14, Write_Enable);
  and and_16 (and_16_out, decoder_1_out15, Write_Enable);
  and and_17 (and_17_out, Write_Enable, decoder_1_out16);
  and and_18 (and_18_out, Write_Enable, decoder_1_out17);
  and and_19 (and_19_out, decoder_1_out18, Write_Enable);
  and and_20 (and_20_out, Write_Enable, decoder_1_out19);
  and and_21 (and_21_out, decoder_1_out20, Write_Enable);
  and and_22 (and_22_out, decoder_1_out21, Write_Enable);
  and and_23 (and_23_out, decoder_1_out22, Write_Enable);
  and and_24 (and_24_out, decoder_1_out23, Write_Enable);
  and and_25 (and_25_out, decoder_1_out24, Write_Enable);
  and and_26 (and_26_out, Write_Enable, decoder_1_out25);
  and and_27 (and_27_out, decoder_1_out26, Write_Enable);
  and and_28 (and_28_out, decoder_1_out27, Write_Enable);
  and and_29 (and_29_out, Write_Enable, decoder_1_out28);
  and and_30 (and_30_out, decoder_1_out29, Write_Enable);
  and and_31 (and_31_out, Write_Enable, decoder_1_out30);
  and and_32 (and_32_out, decoder_1_out31, Write_Enable);
  Register #(.width(32), .Select("high")) _0 (
    .D(Din), .en(and_1_out), .Q(_0_q), .clk(and_1_out), .preset(undriven));  // open: clr, cs
  Register #(.width(32), .Select("high")) _1 (
    .D(Din), .en(and_2_out), .Q(_1_q), .clk(and_2_out), .clr(1'b0), .cs(1'b1), .preset(1'b0));
  Register #(.width(32), .Select("high")) _2 (
    .D(Din), .en(and_3_out), .Q(_2_q), .clk(and_3_out), .clr(1'b0), .cs(1'b1), .preset(1'b0));
  Register #(.width(32), .Select("high")) _3 (
    .D(Din), .en(and_4_out), .Q(_3_q), .clk(and_4_out), .clr(1'b0), .cs(1'b1), .preset(1'b0));
  Register #(.width(32), .Select("high")) _4 (
    .D(Din), .en(and_5_out), .Q(_4_q), .clk(and_5_out), .clr(1'b0), .cs(1'b1), .preset(1'b0));
  Register #(.width(32), .Select("high")) _5 (
    .D(Din), .en(and_6_out), .Q(_5_q), .clk(Clock), .clr(1'b0), .cs(1'b1), .preset(1'b0));
  Register #(.width(32), .Select("high")) _6 (
    .D(Din), .en(and_7_out), .Q(_6_q), .clk(Clock), .clr(1'b0), .cs(1'b1), .preset(1'b0));
  Register #(.width(32), .Select("high")) _7 (
    .D(Din), .en(and_8_out), .Q(_7_q), .clk(Clock), .clr(1'b0), .cs(1'b1), .preset(1'b0));
  Register #(.width(32), .Select("high")) _8 (
    .D(Din), .en(and_9_out), .Q(_8_q), .clk(Clock), .clr(1'b0), .cs(1'b1), .preset(1'b0));
  Register #(.width(32), .Select("high")) _9 (
    .D(Din), .en(and_10_out), .Q(_9_q), .clk(Clock), .clr(1'b0), .cs(1'b1), .preset(1'b0));
  Register #(.width(32), .Select("high")) register_1 (
    .D(Din), .en(and_11_out), .Q(register_1_q), .clk(Clock), .clr(1'b0), .cs(1'b1), .preset(1'b0));
  Register #(.width(32), .Select("high")) register_2 (
    .D(Din), .en(and_12_out), .Q(register_2_q), .clk(Clock), .clr(1'b0), .cs(1'b1), .preset(1'b0));
  Register #(.width(32), .Select("high")) register_3 (
    .D(Din), .en(and_13_out), .Q(register_3_q), .clk(Clock), .clr(1'b0), .cs(1'b1), .preset(1'b0));
  Register #(.width(32), .Select("high")) register_4 (
    .D(Din), .en(and_14_out), .Q(register_4_q), .clk(Clock), .clr(1'b0), .cs(1'b1), .preset(1'b0));
  Register #(.width(32), .Select("high")) register_5 (
    .D(Din), .en(and_15_out), .Q(register_5_q), .clk(Clock), .clr(1'b0), .cs(1'b1), .preset(1'b0));
  Register #(.width(32), .Select("high")) register_6 (
    .D(Din), .en(and_16_out), .Q(register_6_q), .clk(Clock), .clr(1'b0), .cs(1'b1), .preset(1'b0));
  Register #(.width(32), .Select("high")) register_7 (
    .D(Din), .en(and_17_out), .Q(register_7_q), .clk(Clock), .clr(1'b0), .cs(1'b1), .preset(1'b0));
  Register #(.width(32), .Select("high")) register_8 (
    .D(Din), .en(and_18_out), .Q(register_8_q), .clk(Clock), .clr(1'b0), .cs(1'b1), .preset(1'b0));
  Register #(.width(32), .Select("high")) register_9 (
    .D(Din), .en(and_19_out), .Q(register_9_q), .clk(Clock), .clr(1'b0), .cs(1'b1), .preset(1'b0));
  Register #(.width(32), .Select("high")) register_10 (
    .D(Din), .en(and_20_out), .Q(register_10_q), .clk(Clock), .clr(1'b0), .cs(1'b1), .preset(1'b0));
  Register #(.width(32), .Select("high")) register_11 (
    .D(Din), .en(and_21_out), .Q(register_11_q), .clk(Clock), .clr(1'b0), .cs(1'b1), .preset(1'b0));
  Register #(.width(32), .Select("high")) register_12 (
    .D(Din), .en(and_22_out), .Q(register_12_q), .clk(Clock), .clr(1'b0), .cs(1'b1), .preset(1'b0));
  Register #(.width(32), .Select("high")) register_13 (
    .D(Din), .en(and_23_out), .Q(register_13_q), .clk(Clock), .clr(1'b0), .cs(1'b1), .preset(1'b0));
  Register #(.width(32), .Select("high")) register_14 (
    .D(Din), .en(and_24_out), .Q(register_14_q), .clk(Clock), .clr(1'b0), .cs(1'b1), .preset(1'b0));
  Register #(.width(32), .Select("high")) register_15 (
    .D(Din), .en(and_25_out), .Q(register_15_q), .clk(Clock), .clr(1'b0), .cs(1'b1), .preset(1'b0));
  Register #(.width(32), .Select("high")) register_16 (
    .D(Din), .en(and_26_out), .Q(register_16_q), .clk(Clock), .clr(1'b0), .cs(1'b1), .preset(1'b0));
  Register #(.width(32), .Select("high")) register_17 (
    .D(Din), .en(and_27_out), .Q(register_17_q), .clk(Clock), .clr(1'b0), .cs(1'b1), .preset(1'b0));
  Register #(.width(32), .Select("high")) register_18 (
    .D(Din), .en(and_28_out), .Q(register_18_q), .clk(Clock), .clr(1'b0), .cs(1'b1), .preset(1'b0));
  Register #(.width(32), .Select("high")) register_19 (
    .D(Din), .en(and_29_out), .Q(register_19_q), .clk(Clock), .clr(1'b0), .cs(1'b1), .preset(1'b0));
  Register #(.width(32), .Select("high")) register_20 (
    .D(Din), .en(and_30_out), .Q(register_20_q), .clk(Clock), .clr(1'b0), .cs(1'b1), .preset(1'b0));
  Register #(.width(32), .Select("high")) register_21 (
    .D(Din), .en(and_31_out), .Q(register_21_q), .clk(Clock), .clr(1'b0), .cs(1'b1), .preset(1'b0));
  Register #(.width(32), .Select("high")) register_22 (
    .D(Din), .en(and_32_out), .Q(register_22_q), .clk(Clock), .clr(1'b0), .cs(1'b1), .preset(1'b0));
  Multiplexer #(.select(5), .width(32), .enable("false")) multiplexer_1 (
    .in0(_0_q), .in1(_1_q), .in2(_2_q), .in3(_3_q), .in4(_4_q), .in5(_5_q), .in6(_6_q), .in7(_7_q),
    .in8(_8_q), .in9(_9_q), .in10(register_1_q), .in11(register_2_q), .in12(register_3_q),
    .in13(register_4_q), .in14(register_5_q), .in15(register_6_q), .in16(register_7_q), .in17(register_8_q),
    .in18(register_9_q), .in19(register_10_q), .in20(register_11_q), .in21(register_12_q),
    .in22(register_13_q), .in23(register_14_q), .in24(register_15_q), .in25(register_16_q),
    .in26(register_17_q), .in27(register_18_q), .in28(register_19_q), .in29(register_20_q),
    .in30(register_21_q), .in31(register_22_q), .out(Reg1Out), .sel(R1_num));
  Multiplexer #(.select(5), .width(32), .enable("false")) multiplexer_2 (
    .in0(_0_q), .in1(_1_q), .in2(_2_q), .in3(_3_q), .in4(_4_q), .in5(_5_q), .in6(_6_q), .in7(_7_q),
    .in8(_8_q), .in9(_9_q), .in10(register_1_q), .in11(register_2_q), .in12(register_3_q),
    .in13(register_4_q), .in14(register_5_q), .in15(register_6_q), .in16(register_7_q), .in17(register_8_q),
    .in18(register_9_q), .in19(register_10_q), .in20(register_11_q), .in21(register_12_q),
    .in22(register_13_q), .in23(register_14_q), .in24(register_15_q), .in25(register_16_q),
    .in26(register_17_q), .in27(register_18_q), .in28(register_19_q), .in29(register_20_q),
    .in30(register_21_q), .in31(register_22_q), .out(Reg2Out), .sel(R2_num));

  // Other names for the same wires on the sheet: CLK = Clock; RA[4:0] = R1_num; RB[4:0] = R2_num; RDA[31:0] = Reg1Out;
  //   RDB[31:0] = Reg2Out; RW[4:0] = Write_Reg_num; WE = Write_Enable

  // Notes on the sheet:
  //   输入引脚
  //   请勿修改引脚名称、电路名称及电路封装外观
  //   提示：使用译码器、多路选择器和32位寄存器及逻辑门实现寄存器堆，禁止直接使用存储器组件。
  //   输出引脚
endmodule
