// Logisim project lab3.5.circ as structural Verilog: 1 circuit, main circuit main
module main (
  input  CLK,
  input  LD,
  input  [3:0] HH1,
  input  [3:0] HH0,
  input  [3:0] MM1,
  input  [3:0] MM0,
  input  [3:0] SS1,
  input  [3:0] SS0,
  output [3:0] HH_H,
  output [3:0] HH_L,
  output [3:0] MM_H,
  output [3:0] MM_L,
  output [3:0] SS_H,
  output [3:0] SS_L,
  output LED_R,
  output LED_G,
  output LED_B,
  output INErr
);

  wire and_1_out, and_2_out, and_4_out, and_5_out, and_6_out, and_7_out, and_8_out, and_9_out, and_11_out,
       and_12_out, and_13_out, and_14_out, buzzer_1_p2, comparator_1_eq, comparator_1_gt, comparator_2_gt,
       comparator_3_gt, comparator_4_gt, comparator_5_gt, comparator_6_gt, comparator_7_gt, comparator_10_eq,
       comparator_11_eq, comparator_12_eq, comparator_13_eq, comparator_14_eq, comparator_15_eq, LED_EN,
       not_1_out, or_1_out, or_2_out, or_3_out, START, STOP;
  wire [3:0] cntr4u_4_q0;

  and and_1 (and_1_out, LD, ~INErr);  // AND_Gate
  and and_2 (and_2_out, and_6_out, and_12_out);
  and and_3 (LED_EN, and_13_out, and_7_out);
  and and_4 (and_4_out, and_8_out, and_14_out);
  Comparator #(.width(4), .mode("unsigned")) comparator_1 (
    .a(HH1), .b(4'b0010), .gt(comparator_1_gt), .eq(comparator_1_eq));  // open: lt
  Comparator #(.width(4), .mode("unsigned")) comparator_2 (.a(HH0), .b(4'b0011), .gt(comparator_2_gt));  // open: eq, lt
  Comparator #(.width(4), .mode("unsigned")) comparator_3 (.a(HH0), .b(4'b1001), .gt(comparator_3_gt));  // open: eq, lt
  Comparator #(.width(4), .mode("unsigned")) comparator_4 (.a(MM1), .b(4'b0101), .gt(comparator_4_gt));  // open: eq, lt
  Comparator #(.width(4), .mode("unsigned")) comparator_5 (.a(MM0), .b(4'b1001), .gt(comparator_5_gt));  // open: eq, lt
  Comparator #(.width(4), .mode("unsigned")) comparator_6 (.a(SS1), .b(4'b0101), .gt(comparator_6_gt));  // open: eq, lt
  Comparator #(.width(4), .mode("unsigned")) comparator_7 (.a(SS0), .b(4'b1001), .gt(comparator_7_gt));  // open: eq, lt
  and and_5 (and_5_out, STOP, START);
  or or_1 (or_1_out, LED_EN, and_5_out);
  Hex_Digit_Display hex_digit_display_1 (.value(HH_H));  // open: dp
  CNTR4U cntr4u_1 (
    .CLK(CLK), .LD(and_1_out), .CLR(and_2_out), .Q0(HH_H[0]), .Q1(HH_H[1]), .D0(HH1[0]), .D1(HH1[1]),
    .D2(HH1[2]), .Q2(HH_H[2]), .Q3(HH_H[3]), .D3(HH1[3]), .ENP(and_11_out), .ENT(and_11_out));  // open: RCO
  and and_6 (and_6_out, ~HH_H[0], HH_H[1], ~HH_H[2], ~HH_H[3]);  // AND_Gate
  CNTR4U cntr4u_2 (
    .CLK(CLK), .LD(and_1_out), .CLR(LED_EN), .Q0(MM_H[0]), .Q1(MM_H[1]), .D0(MM1[0]), .D1(MM1[1]),
    .D2(MM1[2]), .Q2(MM_H[2]), .Q3(MM_H[3]), .D3(MM1[3]), .ENP(and_13_out), .ENT(and_13_out));  // open: RCO
  and and_7 (and_7_out, MM_H[0], ~MM_H[1], MM_H[2], ~MM_H[3]);  // AND_Gate
  CNTR4U cntr4u_3 (
    .CLK(CLK), .LD(and_1_out), .CLR(and_4_out), .Q0(SS_H[0]), .Q1(SS_H[1]), .D0(SS1[0]), .D1(SS1[1]),
    .D2(SS1[2]), .Q2(SS_H[2]), .Q3(SS_H[3]), .D3(SS1[3]), .ENP(and_14_out), .ENT(and_14_out));  // open: RCO
  and and_8 (and_8_out, SS_H[0], ~SS_H[1], SS_H[2], ~SS_H[3]);  // AND_Gate
  and and_9 (and_9_out, comparator_1_eq, comparator_2_gt);
  not not_1 (not_1_out, or_1_out);
  Hex_Digit_Display hex_digit_display_2 (.value(HH_L), .dp(1'b1));
  Hex_Digit_Display hex_digit_display_3 (.value(MM_H));  // open: dp
  or or_2 (or_2_out, comparator_1_gt, and_9_out, comparator_3_gt, comparator_4_gt, comparator_5_gt, comparator_6_gt, comparator_7_gt);
  CNTR4U cntr4u_4 (
    .CLK(CLK), .LD(LED_EN), .CLR(not_1_out), .Q0(cntr4u_4_q0[0]), .Q1(cntr4u_4_q0[1]), .D0(LED_EN),
    .D1(1'b0), .D2(1'b0), .Q2(LED_B), .Q3(cntr4u_4_q0[3]), .D3(1'b0), .ENP(and_5_out), .ENT(and_5_out));  // open: RCO
  Hex_Digit_Display hex_digit_display_4 (.value(MM_L), .dp(1'b1));
  Hex_Digit_Display hex_digit_display_5 (.value(SS_H));  // open: dp
  or or_3 (or_3_out, and_2_out, and_11_out);
  and and_10 (INErr, or_2_out, LD);
  Hex_Digit_Display hex_digit_display_6 (.value(SS_L), .dp(1'b1));
  and and_11 (and_11_out, HH_L[0], ~HH_L[1], ~HH_L[2], HH_L[3], LED_EN);  // AND_Gate
  and and_12 (and_12_out, HH_L[0], HH_L[1], ~HH_L[2], ~HH_L[3], LED_EN);  // AND_Gate
  and and_13 (and_13_out, MM_L[0], ~MM_L[1], ~MM_L[2], MM_L[3], and_4_out);  // AND_Gate
  CNTR4U cntr4u_5 (
    .CLK(CLK), .LD(and_1_out), .CLR(or_3_out), .Q0(HH_L[0]), .Q1(HH_L[1]), .D0(HH0[0]), .D1(HH0[1]),
    .D2(HH0[2]), .Q2(HH_L[2]), .Q3(HH_L[3]), .D3(HH0[3]), .ENP(LED_EN), .ENT(LED_EN));  // open: RCO
  CNTR4U cntr4u_6 (
    .CLK(CLK), .LD(and_1_out), .CLR(and_13_out), .Q0(MM_L[0]), .Q1(MM_L[1]), .D0(MM0[0]), .D1(MM0[1]),
    .D2(MM0[2]), .Q2(MM_L[2]), .Q3(MM_L[3]), .D3(MM0[3]), .ENP(and_4_out), .ENT(and_4_out));  // open: RCO
  CNTR4U cntr4u_7 (
    .CLK(CLK), .LD(and_1_out), .CLR(and_14_out), .Q0(SS_L[0]), .Q1(SS_L[1]), .D0(SS0[0]), .D1(SS0[1]),
    .D2(SS0[2]), .Q2(SS_L[2]), .Q3(SS_L[3]), .D3(SS0[3]), .ENP(1'b1), .ENT(1'b1));  // open: RCO
  and and_14 (and_14_out, SS_L[0], ~SS_L[1], ~SS_L[2], SS_L[3]);  // AND_Gate
  Comparator #(.width(4), .mode("unsigned")) comparator_8 (
    .a({cntr4u_4_q0[3], LED_B, cntr4u_4_q0[1:0]}), .b(4'b0000), .gt(START));  // open: eq, lt
  Comparator #(.width(4), .mode("unsigned")) comparator_9 (
    .a({cntr4u_4_q0[3], LED_B, cntr4u_4_q0[1:0]}), .b(4'b1010), .lt(STOP));  // open: gt, eq
  xor xor_1 (LED_R, cntr4u_4_q0[0], cntr4u_4_q0[1]);
  xor xor_2 (LED_G, cntr4u_4_q0[1], LED_B);
  // RGBLed RGBLED: pin names not known; wires that end beside it: LED_R, LED_G, LED_B, HH_L
  Comparator #(.width(4), .mode("unsigned")) comparator_10 (
    .a(HH_H), .b(4'b0010), .eq(comparator_10_eq));  // open: gt, lt
  Comparator #(.width(4), .mode("unsigned")) comparator_11 (
    .a(HH_L), .b(4'b0011), .eq(comparator_11_eq));  // open: gt, lt
  Comparator #(.width(4), .mode("unsigned")) comparator_12 (
    .a(MM_H), .b(4'b0101), .eq(comparator_12_eq));  // open: gt, lt
  Comparator #(.width(4), .mode("unsigned")) comparator_13 (
    .a(MM_L), .b(4'b1001), .eq(comparator_13_eq));  // open: gt, lt
  Comparator #(.width(4), .mode("unsigned")) comparator_14 (
    .a(SS_H), .b(4'b0101), .eq(comparator_14_eq));  // open: gt, lt
  Comparator #(.width(4), .mode("unsigned")) comparator_15 (
    .a(SS_L), .b(4'b1001), .eq(comparator_15_eq));  // open: gt, lt
  // Buzzer #(.vol_width(5)) buzzer_1: pin names not known; wires that end beside it: 14'h3a7, buzzer_1_p2, 5'b01010
  and and_15 (buzzer_1_p2, comparator_10_eq, comparator_11_eq, comparator_12_eq, comparator_13_eq, comparator_15_eq, comparator_14_eq);

  // Other names for the same wires on the sheet: H0[3:0] = HH_L; H1[3:0] = HH_H; M0[3:0] = MM_L; M1[3:0] = MM_H;
  //   S0[3:0] = SS_L; S1[3:0] = SS_H

  // Notes on the sheet:
  //   设置初始时间BCD码
  //   输入信号
  //   请勿修改引脚名称、电路名称及电路封装外观
  //   000 001 011 010 110 111 101 100
  //   数字时钟
  //   提示：使用4位二进制加法计数器子电路、比较器和独立逻辑门组件实现数字时钟。
  //   在载入有效时，检测设置数据错误
  //   生成三色LED显示信号，持续10个时钟周期
  //   频率
  //   音量
endmodule
