// Logisim project 32-division.circ as structural Verilog: 2 circuits, main circuit main
module main (
  input  [15:0] in_1,
  input  in_2,
  input  [15:0] in_3,
  output [15:0] out_4,
  output [15:0] out_5
);

  wire and_1_out, clk, LOAD, not_1_out, not_2_out, STOP, subtractor_1_bout, ZF;
  wire [0:0] not_3_out;
  wire [7:0] counter_1_q;
  wire [15:0] multiplexer_4_out;
  wire [31:0] bit_extender_1_out, multiplexer_1_out, multiplexer_2_out, multiplexer_3_out, register_1_q,
       shifter_1_out, subtractor_1_out;
  wire [31:16] register_2_q;

  Clock clock_1 (.out(clk));
  Shifter #(.width(32), .shift("lr")) shifter_1 (.in(multiplexer_2_out), .\dist (5'b00001), .out(shifter_1_out));
  Comparator #(.width(16)) comparator_1 (.a(in_3), .b({16{1'b0}}), .eq(ZF));  // open: gt, lt
  Hex_Digit_Display hex_digit_display_1 (.value(in_1[15:12]));  // open: dp
  Multiplexer #(.width(32), .enable("false")) multiplexer_1 (
    .in0(multiplexer_3_out), .in1(bit_extender_1_out), .out(multiplexer_1_out), .sel(LOAD));
  assign bit_extender_1_out = {{16{1'b0}}, in_1};  // Bit_Extender bit_extender_1
  Register #(.width(32), .Select("low")) register_1 (
    .D(shifter_1_out), .en(and_1_out), .Q(register_1_q), .clk(clk), .clr(in_2));
  Hex_Digit_Display hex_digit_display_2 (.value(in_1[11:8]));  // open: dp
  Register #(.width(32), .Select("low")) register_2 (
    .D(multiplexer_1_out), .en(and_1_out), .Q({register_2_q, out_4}), .clk(clk), .clr(in_2));
  Multiplexer #(.width(32), .enable("false")) multiplexer_2 (
    .in0(register_1_q), .in1({in_3, {16{1'b0}}}), .out(multiplexer_2_out), .sel(LOAD));
  Hex_Digit_Display hex_digit_display_3 (.value(in_1[3:0]));  // open: dp
  Hex_Digit_Display hex_digit_display_4 (.value(in_1[7:4]));  // open: dp
  and and_1 (and_1_out, not_1_out, not_2_out);
  Hex_Digit_Display hex_digit_display_5 (.value(in_3[15:12]));  // open: dp
  Subtractor #(.width(32)) subtractor_1 (
    .a({register_2_q, out_4}), .b(multiplexer_2_out), .out(subtractor_1_out), .bout(subtractor_1_bout));  // open: bin
  not not_1 (not_1_out, STOP);
  not not_2 (not_2_out, ZF);
  not not_3 (not_3_out[0], subtractor_1_bout);
  Hex_Digit_Display hex_digit_display_6 (.value(in_3[11:8]));  // open: dp
  Multiplexer #(.width(32), .enable("false")) multiplexer_3 (
    .in0(subtractor_1_out), .in1({register_2_q, out_4}), .out(multiplexer_3_out), .sel(subtractor_1_bout));
  Multiplexer #(.width(16), .enable("false")) multiplexer_4 (
    .in0(out_5), .in1({16{1'b0}}), .out(multiplexer_4_out), .sel(LOAD));
  Hex_Digit_Display hex_digit_display_7 (.value(in_3[7:4]));  // open: dp
  Hex_Digit_Display hex_digit_display_8 (.value(in_3[3:0]));  // open: dp
  Hex_Digit_Display hex_digit_display_9 (.value(out_5[15:12]));  // open: dp
  Counter counter_1 (
    .D({8{1'b0}}), .count(and_1_out), .Q(counter_1_q), .clk(clk), .clr(in_2), .down(1'b0));  // open: load, carry, preset
  Hex_Digit_Display hex_digit_display_10 (.value(out_5[7:4]));  // open: dp
  Hex_Digit_Display hex_digit_display_11 (.value(out_5[11:8]));  // open: dp
  Comparator comparator_2 (.a({8{1'b0}}), .b(counter_1_q), .eq(LOAD));  // open: gt, lt
  Comparator comparator_3 (.a(counter_1_q), .b(8'h11), .eq(STOP));  // open: gt, lt
  Register #(.width(16), .Select("low")) register_3 (
    .D({multiplexer_4_out[14:0], not_3_out[0]}), .en(and_1_out), .Q(out_5), .clk(clk), .clr(in_2));
  Hex_Digit_Display hex_digit_display_12 (.value(out_5[3:0]));  // open: dp
  Hex_Digit_Display hex_digit_display_13 (.value(counter_1_q[7:4]));  // open: dp
  Hex_Digit_Display hex_digit_display_14 (.value(counter_1_q[3:0]));  // open: dp
  Hex_Digit_Display hex_digit_display_15 (.value(out_4[15:12]));  // open: dp
  Hex_Digit_Display hex_digit_display_16 (.value(out_4[11:8]));  // open: dp
  Hex_Digit_Display hex_digit_display_17 (.value(out_4[7:4]));  // open: dp
  Hex_Digit_Display hex_digit_display_18 (.value(out_4[3:0]));  // open: dp

  // Other names for the same wires on the sheet: 除数[15:0] = in_3; 余数[15:0] = out_4; RST = in_2; 商[15:0] = out_5;
  //   被除数[15:0] = in_1

  // Notes on the sheet:
  //   ➗
  //   =
  //   余
endmodule

module test (
  input  in_1,
  input  [31:0] in_2,
  input  [31:0] in_3,
  output [31:0] out_4,
  output [31:0] out_5
);

  wire clk, LOAD, not_1_out, not_3_out, STOP, subtractor_1_bout;
  wire [0:0] not_2_out;
  wire [7:0] counter_1_q;
  wire [31:0] multiplexer_1_out, multiplexer_2_out, multiplexer_3_out, multiplexer_4_out, register_1_q,
       shifter_1_out, subtractor_1_out;

  Hex_Digit_Display hex_digit_display_1 (.value(in_2[31:28]));  // open: dp
  Hex_Digit_Display hex_digit_display_2 (.value(in_2[27:24]));  // open: dp
  Clock clock_1 (.out(clk));
  Shifter #(.width(32), .shift("lr")) shifter_1 (.in(multiplexer_2_out), .\dist (5'b00001), .out(shifter_1_out));
  Hex_Digit_Display hex_digit_display_3 (.value(in_2[19:16]));  // open: dp
  Hex_Digit_Display hex_digit_display_4 (.value(in_2[23:20]));  // open: dp
  Multiplexer #(.width(32), .enable("false")) multiplexer_1 (
    .in0(multiplexer_3_out), .in1(in_2), .out(multiplexer_1_out), .sel(LOAD));
  Register #(.width(32), .Select("low")) register_1 (
    .D(shifter_1_out), .en(not_1_out), .Q(register_1_q), .clk(clk), .clr(in_1));
  Hex_Digit_Display hex_digit_display_5 (.value(in_2[15:12]));  // open: dp
  Hex_Digit_Display hex_digit_display_6 (.value(in_2[11:8]));  // open: dp
  Register #(.width(32), .Select("low")) register_2 (
    .D(multiplexer_1_out), .en(not_1_out), .Q(out_5), .clk(clk), .clr(in_1));
  Multiplexer #(.width(32), .enable("false")) multiplexer_2 (
    .in0(register_1_q), .in1(in_3), .out(multiplexer_2_out), .sel(LOAD));
  Hex_Digit_Display hex_digit_display_7 (.value(in_2[7:4]));  // open: dp
  Hex_Digit_Display hex_digit_display_8 (.value(in_2[3:0]));  // open: dp
  Subtractor #(.width(32)) subtractor_1 (
    .a(out_5), .b(multiplexer_2_out), .out(subtractor_1_out), .bout(subtractor_1_bout));  // open: bin
  not not_1 (not_1_out, STOP);
  not not_2 (not_2_out[0], subtractor_1_bout);
  Hex_Digit_Display hex_digit_display_9 (.value(in_3[31:28]));  // open: dp
  Multiplexer #(.width(32), .enable("false")) multiplexer_3 (
    .in0(subtractor_1_out), .in1(out_5), .out(multiplexer_3_out), .sel(subtractor_1_bout));
  Multiplexer #(.width(32), .enable("false")) multiplexer_4 (
    .in0(out_4), .in1({32{1'b0}}), .out(multiplexer_4_out), .sel(LOAD));
  Hex_Digit_Display hex_digit_display_10 (.value(in_3[23:20]));  // open: dp
  Hex_Digit_Display hex_digit_display_11 (.value(in_3[27:24]));  // open: dp
  Hex_Digit_Display hex_digit_display_12 (.value(in_3[19:16]));  // open: dp
  not not_3 (not_3_out, STOP);
  Counter counter_1 (
    .D({8{1'b0}}), .count(not_3_out), .Q(counter_1_q), .clk(clk), .clr(in_1), .down(1'b0));  // open: load, carry, preset
  Hex_Digit_Display hex_digit_display_13 (.value(in_3[15:12]));  // open: dp
  Hex_Digit_Display hex_digit_display_14 (.value(in_3[11:8]));  // open: dp
  Register #(.width(32), .Select("low")) register_3 (
    .D({multiplexer_4_out[30:0], not_2_out[0]}), .en(not_1_out), .Q(out_4), .clk(clk), .clr(in_1));
  Hex_Digit_Display hex_digit_display_15 (.value(in_3[3:0]));  // open: dp
  Hex_Digit_Display hex_digit_display_16 (.value(in_3[7:4]));  // open: dp
  Hex_Digit_Display hex_digit_display_17 (.value(counter_1_q[3:0]));  // open: dp
  Hex_Digit_Display hex_digit_display_18 (.value(counter_1_q[7:4]));  // open: dp
  Comparator comparator_1 (.a({8{1'b0}}), .b(counter_1_q), .eq(LOAD));  // open: gt, lt
  Comparator comparator_2 (.a(counter_1_q), .b(8'h21), .eq(STOP));  // open: gt, lt
  Hex_Digit_Display hex_digit_display_19 (.value(out_4[27:24]));  // open: dp
  Hex_Digit_Display hex_digit_display_20 (.value(out_4[31:28]));  // open: dp
  Hex_Digit_Display hex_digit_display_21 (.value(out_4[23:20]));  // open: dp
  Hex_Digit_Display hex_digit_display_22 (.value(out_4[19:16]));  // open: dp
  Hex_Digit_Display hex_digit_display_23 (.value(out_4[15:12]));  // open: dp
  Hex_Digit_Display hex_digit_display_24 (.value(out_4[11:8]));  // open: dp
  Hex_Digit_Display hex_digit_display_25 (.value(out_4[7:4]));  // open: dp
  Hex_Digit_Display hex_digit_display_26 (.value(out_4[3:0]));  // open: dp
  Hex_Digit_Display hex_digit_display_27 (.value(out_5[27:24]));  // open: dp
  Hex_Digit_Display hex_digit_display_28 (.value(out_5[31:28]));  // open: dp
  Hex_Digit_Display hex_digit_display_29 (.value(out_5[23:20]));  // open: dp
  Hex_Digit_Display hex_digit_display_30 (.value(out_5[19:16]));  // open: dp
  Hex_Digit_Display hex_digit_display_31 (.value(out_5[15:12]));  // open: dp
  Hex_Digit_Display hex_digit_display_32 (.value(out_5[11:8]));  // open: dp
  Hex_Digit_Display hex_digit_display_33 (.value(out_5[3:0]));  // open: dp
  Hex_Digit_Display hex_digit_display_34 (.value(out_5[7:4]));  // open: dp

  // Other names for the same wires on the sheet: RST = in_1; 余数[31:0] = out_5; 商[31:0] = out_4; 被除数[31:0] = in_2;
  //   除数[31:0] = in_3

  // Notes on the sheet:
  //   ➗
  //   =
  //   test failed
  //   余
endmodule
