// Logisim project lab4.3.circ as structural Verilog: 1 circuit, main circuit Adder32
// 加法器
module Adder32 (
  input  Cin,
  input  [31:0] X,
  input  [31:0] Y,
  output CF,
  output Cout,
  output OF,
  output SF,
  output [31:0] S,
  output ZF
);

  wire and_1_out, and_2_out, main_2_c16, not_1_out, not_2_out, not_3_out, or_3_out, or_4_out;
  wire [3:0] or_1_out, or_2_out;

  lab4_2_main main_1 (.X(X[31:16]), .Y(Y[31:16]), .C0(main_2_c16), .S(S[31:16]), .C16(Cout));  // open: Pg, Gg
  assign or_1_out = S[19:16] | S[23:20] | S[27:24] | S[31:28];  // OR_Gate or_1, 4 bits wide
  assign or_2_out = S[3:0] | S[7:4] | S[11:8] | S[15:12];  // OR_Gate or_2, 4 bits wide
  or or_3 (or_3_out, or_1_out[0], or_1_out[1], or_1_out[2], or_1_out[3]);
  or or_4 (or_4_out, or_2_out[0], or_2_out[1], or_2_out[2], or_2_out[3]);
  lab4_2_main main_2 (.X(X[15:0]), .Y(Y[15:0]), .C0(Cin), .S(S[15:0]), .C16(main_2_c16));  // open: Pg, Gg
  nor nor_1 (ZF, or_3_out, or_4_out);
  // Probe on X
  // Probe on Y
  // Probe on S
  xor xor_1 (CF, Cout, Cin);
  not not_1 (not_1_out, S[31]);
  not not_2 (not_2_out, X[31]);
  not not_3 (not_3_out, Y[31]);
  and and_1 (and_1_out, not_1_out, X[31], Y[31]);
  and and_2 (and_2_out, not_2_out, S[31], not_3_out);
  or or_5 (OF, and_1_out, and_2_out);

  assign SF = S[31];

  // Other names for the same wires on the sheet: S0[15:0] = S[15:0]; S1[15:0] = S[31:16]; X1[15:0] = X[31:16];
  //   Y1[15:0] = Y[31:16]

  // Notes on the sheet:
  //   Cin: pull=down
  //   Y: pull=down
  //   X: pull=down
  //   输入引脚区
  //   输出引脚区
  //   请勿修改引脚名称、电路名称及电路封装外观
  //   提示：使用16位并行加法器子电路实现32位快速加法器
  //   功能说明:32位Adder  S=X+Y，Cout为最高位进位位，Cin为进位输入， S为和，溢出OF、进位CF、零ZF、符号SF。
  //   +
  //   =
  //   无符号加法
endmodule
