// Logisim project lab4.4.circ as structural Verilog: 1 circuit, main circuit main
// 移位器
module main (
  input  [4:0] shamt,
  input  L_R,
  input  A_L,
  input  [31:0] DataIn,
  output [31:0] DataOut
);

  wire [0:0] and_1_out;
  wire [1:0] and_3_out;
  wire [1:1] and_4_out;
  wire [3:0] and_5_out;
  wire [3:3] and_6_out;
  wire [7:0] and_7_out, multiplexer_3_out;
  wire [15:0] and_9_out;
  wire [15:15] and_10_out;
  wire [31:0] multiplexer_1_out, multiplexer_2_out, multiplexer_3_out_2, multiplexer_4_out;
  wire [31:31] and_2_out;

  and and_1 (and_1_out[0], A_L, DataIn[31]);
  and and_2 (and_2_out[31], DataIn[31], A_L);
  Multiplexer #(.select(2), .width(32), .enable("false")) multiplexer_1 (
    .in0(DataIn), .in1(DataIn), .in2({and_2_out[31], DataIn[31:1]}), .in3({DataIn[30:0], and_1_out[0]}),
    .out(multiplexer_1_out), .sel({shamt[0], L_R}));
  assign and_3_out = {2{A_L}} & multiplexer_1_out[31:30];  // AND_Gate and_3, 2 bits wide
  and and_4 (and_4_out[1], multiplexer_1_out[31], A_L);
  Multiplexer #(.select(2), .width(32), .enable("false")) multiplexer_2 (
    .in0(multiplexer_1_out), .in1(multiplexer_1_out), .in2({{2{and_4_out[1]}}, multiplexer_1_out[31:2]}),
    .in3({multiplexer_1_out[29:0], and_3_out}), .out(multiplexer_2_out), .sel({shamt[1], L_R}));
  assign and_5_out = {4{A_L}} & multiplexer_2_out[31:28];  // AND_Gate and_5, 4 bits wide
  and and_6 (and_6_out[3], multiplexer_2_out[31], A_L);
  Multiplexer #(.select(2), .width(32), .enable("false")) multiplexer_3 (
    .in0(multiplexer_2_out), .in1(multiplexer_2_out), .in2({{4{and_6_out[3]}}, multiplexer_2_out[31:4]}),
    .in3({multiplexer_2_out[27:0], and_5_out}), .out({multiplexer_3_out_2[23:0], multiplexer_3_out}),
    .sel({shamt[2], L_R}));
  assign and_7_out = {8{A_L}} & multiplexer_3_out_2[23:16];  // AND_Gate and_7, 8 bits wide
  and and_8 (multiplexer_3_out_2[31], multiplexer_3_out_2[23], A_L);
  Multiplexer #(.select(2), .width(32), .enable("false")) multiplexer_4 (
    .in0({multiplexer_3_out_2[23:0], multiplexer_3_out}),
    .in1({multiplexer_3_out_2[23:0], multiplexer_3_out}),
    .in2({{8{multiplexer_3_out_2[31]}}, multiplexer_3_out_2[23:0]}),
    .in3({multiplexer_3_out_2[15:0], multiplexer_3_out, and_7_out}), .out(multiplexer_4_out),
    .sel({shamt[3], L_R}));
  assign and_9_out = {16{A_L}} & multiplexer_4_out[31:16];  // AND_Gate and_9, 16 bits wide
  and and_10 (and_10_out[15], multiplexer_4_out[31], A_L);
  Multiplexer #(.select(2), .width(32), .enable("false")) multiplexer_5 (
    .in0(multiplexer_4_out), .in1(multiplexer_4_out), .in2({{16{and_10_out[15]}}, multiplexer_4_out[31:16]}),
    .in3({multiplexer_4_out[15:0], and_9_out}), .out(DataOut), .sel({shamt[4], L_R}));

  // Other names for the same wires on the sheet: Din[31:0] = DataIn; Arth_Logic = A_L; Left_Right = L_R;
  //   Dout[31:0] = DataOut

  // Notes on the sheet:
  //   L/R,A/L: 00逻辑右移，01算术右移，10逻辑左移，11：循环左移
  //   输入引脚
  //   请勿修改引脚名称、电路名称及电路封装外观
  //   提示：使用多路选择器、逻辑门实现32位桶形移位器，禁止直接使用移位器组件。
  //   1
  //   对选择器，00/01都不移动；10右移，11左移
  //   输出引脚
  //   2
  //   4
  //   8
  //   16
endmodule
