// Logisim project lab5.2.circ as structural Verilog: 1 circuit, main circuit DataRam
// DataRAM
module DataRam (
  input  CLK,
  input  CLR,
  input  WE,
  input  [2:0] MemOp,
  input  [17:0] Addr,
  input  [31:0] Din,
  output AlignErr,
  output [31:0] DataOut
);

  wire and_1_out, and_2_out, and_3_out, and_4_out, and_5_out, and_6_out, and_7_out, and_8_out, and_9_out,
       and_10_out, and_11_out, and_12_out, and_13_out, and_14_out, and_15_out, and_16_out, Byte1Sel, MemOPwe,
       nor_1_out;
  wire [3:0] Byte0Sel;
  wire [7:0] multiplexer_1_out, multiplexer_2_out, multiplexer_3_out, multiplexer_4_out, multiplexer_5_out,
       ram_4_data;
  wire [31:0] bit_extender_3_out, bit_extender_4_out;
  wire [31:8] bit_extender_1_out, bit_extender_2_out, ram_3_data;

  and and_1 (and_1_out, WE, MemOPwe);
  nor nor_1 (nor_1_out, MemOp[0], MemOp[1], MemOp[2]);
  and and_2 (and_2_out, MemOp[0], ~MemOp[1], MemOp[2]);  // AND_Gate
  and and_3 (and_3_out, ~MemOp[0], MemOp[1], MemOp[2]);  // AND_Gate
  and and_4 (and_4_out, MemOp[0], ~MemOp[1]);  // AND_Gate
  and and_5 (and_5_out, ~MemOp[0], MemOp[1]);  // AND_Gate
  and and_6 (and_6_out, ~Addr[1], ~Addr[0]);  // AND_Gate
  and and_7 (and_7_out, ~Addr[1], Addr[0]);  // AND_Gate
  and and_8 (and_8_out, Addr[1], ~Addr[0]);  // AND_Gate
  and and_9 (and_9_out, Addr[1], Addr[0]);
  Multiplexer #(.select(2), .width(8), .enable("false")) multiplexer_1 (
    .in0(Din[7:0]), .in2(Din[15:8]), .in3(Din[31:24]), .out(multiplexer_1_out),
    .sel({Byte0Sel[2], Byte0Sel[0]}));  // open: in1
  RAM #(.addrWidth(16), .bus("separate"), .Select("high")) ram_1 (
    .addr(Addr[17:2]), .din(multiplexer_1_out), .data(ram_3_data[31:24]), .str(and_1_out), .sel(Byte0Sel[3]),
    .clk(CLK), .clr(CLR));  // open: ld
  Multiplexer #(.width(8), .enable("false")) multiplexer_2 (
    .in0(Din[7:0]), .in1(Din[23:16]), .out(multiplexer_2_out), .sel(Byte0Sel[0]));
  or or_1 (MemOPwe, nor_1_out, and_2_out, and_3_out);
  and and_10 (and_10_out, nor_1_out, and_6_out);
  and and_11 (and_11_out, and_5_out, and_6_out);
  and and_12 (and_12_out, and_4_out, and_6_out);
  and and_13 (and_13_out, and_4_out, and_7_out);
  and and_14 (and_14_out, and_5_out, and_8_out);
  and and_15 (and_15_out, and_8_out, and_4_out);
  and and_16 (and_16_out, and_9_out, and_4_out);
  RAM #(.addrWidth(16), .bus("separate"), .Select("high")) ram_2 (
    .addr(Addr[17:2]), .din(multiplexer_2_out), .data(ram_3_data[23:16]), .str(and_1_out), .sel(Byte0Sel[2]),
    .clk(CLK), .clr(CLR));  // open: ld
  Multiplexer #(.width(8), .enable("false")) multiplexer_3 (
    .in0(Din[7:0]), .in1(Din[15:8]), .out(multiplexer_3_out), .sel(Byte0Sel[0]));
  or or_2 (Byte0Sel[3], and_10_out, and_14_out, and_16_out);
  or or_3 (Byte0Sel[2], and_10_out, and_14_out, and_15_out);
  or or_4 (Byte0Sel[1], and_10_out, and_13_out, and_11_out);
  or or_5 (Byte0Sel[0], and_10_out, and_12_out, and_11_out);
  RAM #(.addrWidth(16), .bus("separate"), .Select("high")) ram_3 (
    .addr(Addr[17:2]), .din(multiplexer_3_out), .data(ram_3_data[15:8]), .str(and_1_out), .sel(Byte0Sel[1]),
    .clk(CLK), .clr(CLR));  // open: ld
  and and_17 (Byte1Sel, ~Byte0Sel[1], Byte0Sel[3]);  // AND_Gate
  Multiplexer #(.width(8), .enable("false")) multiplexer_4 (
    .in0(ram_3_data[15:8]), .in1(ram_3_data[31:24]), .out(multiplexer_4_out), .sel(Byte1Sel));
  nor nor_2 (AlignErr, Byte0Sel[3], Byte0Sel[2], Byte0Sel[0], Byte0Sel[1]);
  RAM #(.addrWidth(16), .bus("separate"), .Select("high")) ram_4 (
    .addr(Addr[17:2]), .din(Din[7:0]), .data(ram_4_data), .str(and_1_out), .sel(Byte0Sel[0]), .clk(CLK),
    .clr(CLR));  // open: ld
  assign bit_extender_1_out = {{16{1'b0}}, multiplexer_4_out};  // Bit_Extender bit_extender_1
  assign bit_extender_2_out = {{16{multiplexer_4_out[7]}}, multiplexer_4_out};  // Bit_Extender bit_extender_2
  Multiplexer #(.select(4), .width(8), .enable("false")) multiplexer_5 (
    .in1(ram_4_data), .in2(ram_3_data[15:8]), .in3(ram_4_data), .in4(ram_3_data[23:16]),
    .in8(ram_3_data[31:24]), .in12(ram_3_data[23:16]), .in15(ram_4_data), .out(multiplexer_5_out),
    .sel(Byte0Sel));  // open: in0, in5, in6, in7, in9, in10, in11, in13, in14
  assign bit_extender_3_out = {{24{1'b0}}, multiplexer_5_out};  // Bit_Extender bit_extender_3
  assign bit_extender_4_out = {{24{multiplexer_5_out[7]}}, multiplexer_5_out};  // Bit_Extender bit_extender_4
  Multiplexer #(.select(3), .width(32), .enable("false")) multiplexer_6 (
    .in0({ram_3_data, multiplexer_5_out}), .in1(bit_extender_3_out),
    .in2({bit_extender_1_out, multiplexer_5_out}), .in4({ram_3_data, multiplexer_5_out}),
    .in5(bit_extender_4_out), .in6({bit_extender_2_out, multiplexer_5_out}), .out(DataOut), .sel(MemOp));  // open: in3, in7

  // Other names for the same wires on the sheet: ramAddr[15:0] = Addr[17:2];
  //   Byte3Sel[1:0] = {Byte0Sel[2], Byte0Sel[0]}; SEL0 = Byte0Sel[0]; SEL1 = Byte0Sel[1]; SEL2 = Byte0Sel[2];
  //   SEL3 = Byte0Sel[3]; Dout[31:0] = DataOut

  // Notes on the sheet:
  //   输入引脚
  //   请勿修改引脚名称、电路名称及电路封装外观
  //   为了后续实验中的引用，不要修改MemOp的编码定义、引脚名称和在布局中的位置。
  //   32位数据存储器，按字节分4片存储，可按照字节、半字和字进行存储；读取字节或半字时，支持0扩展和符号位扩展。
  //   输出引脚
endmodule
