// Logisim project lab5.5.circ as structural Verilog: 15 circuits, main circuit main
module main (
  input  [2:0] ExtOp,
  input  [2:0] MemOp,
  input  RegWr,
  input  ALUASrc,
  input  MemWr,
  input  [1:0] ALUBSrc,
  input  [31:0] Initial_Address,
  input  [3:0] ALUctr,
  input  MemtoReg,
  input  [2:0] BandJ,
  input  clk,
  input  ReSet,
  output [31:0] PC,
  output [31:0] BusW,
  output [31:0] Din,
  output NPCASrc,
  output NPCBSrc
);

  wire alu_1_zero, clock_1_out;
  wire [17:0] alu_1_s;
  wire [31:0] dataram_1_dataout, idu_1_busa, idu_1_dataa, idu_1_datab, idu_1_imm, rom_1_data;
  wire [31:18] alu_1_s_2;

  Clock clock_1 (.out(clock_1_out));
  IFU ifu_1 (
    .CLK(clk), .Reset(ReSet), .NxtASrc(NPCASrc), .NxtBSrc(NPCBSrc), .Initial_Address(Initial_Address),
    .Imm(idu_1_imm), .BusA(idu_1_busa), .PC(PC));
  ROM #(.addrWidth(16), .dataWidth(32), .Select("high")) rom_1 (.addr(PC[17:2]), .data(rom_1_data), .sel(1'b1));
  IDU idu_1 (
    .ExtOp(ExtOp), .RegWr(RegWr), .Imm(idu_1_imm), .ALUASrc(ALUASrc), .ALUBSrc(ALUBSrc), .CLK(clk),
    .IR(rom_1_data), .BusW(BusW), .PC(PC), .DataA(idu_1_dataa), .DataB(idu_1_datab), .BusA(idu_1_busa),
    .BusB(Din));  // open: OpCode, Funct3, Funct7
  ALU alu_1 (.A(idu_1_dataa), .B(idu_1_datab), .ALUctr(ALUctr), .S({alu_1_s_2, alu_1_s}), .Zero(alu_1_zero));
  BandJ bandj_1 (.Branch(BandJ), .NxtASrc(NPCASrc), .Zero(alu_1_zero), .NxtBSrc(NPCBSrc), .Result0(alu_1_s[0]));
  DataRAM dataram_1 (
    .Addr(alu_1_s), .Din(Din), .CLK(clk), .CLR(ReSet), .WE(MemWr), .MemOp(MemOp), .DataOut(dataram_1_dataout));  // open: AlignErr
  Multiplexer #(.width(32), .enable("false")) multiplexer_1 (
    .in0({alu_1_s_2, alu_1_s}), .in1(dataram_1_dataout), .out(BusW), .sel(MemtoReg));

  // Other names for the same wires on the sheet: Init_Addr[31:0] = Initial_Address

  // Notes on the sheet:
  //   ALUASrc: pull=down
  //   ALUctr: pull=down
  //   BandJ: pull=down
  //   ALUBSrc: pull=down
  //   NPCASrc: pull=down
  //   ExtOp: pull=down
  //   NPCBSrc: pull=down
  //   RegWr: pull=down
  //   输入信号
  //   请勿修改引脚名称、电路名称及电路封装外观
  //   为了后续实验中的引用，不要修改控制信号的编码定义、引脚名称和在布局中的位置。
  //   指令存储器和数据存储器数据位都是32位，指令存储器编址以字为单位，数据存储器编址以字节为单位。
  //   32位数据存储器，按字节分4片存储，可按照字节、半字和字进行存储；读取字节或半字时，支持0扩展和符号位扩展。
  //   contents of rom_1 (hex, n*v repeats v):
  //   8000ef ffdff06f 100013 deadc2b7 eef28293 52d333 135313 4052d3b3 529e33 1e1e13 6e0eb3 1000513 5500a3
  //   551223 551323 552423 150483 154903 451983 655a03 452a83 a55b03 ffff0bb7 17afc33 16c6cb3 fb9e92e3 73
  //   输出信号
endmodule

module BandJ (
  input  [2:0] Branch,
  input  Zero,
  input  Result0,
  output NxtASrc,
  output NxtBSrc
);

  wire not_1_out, not_2_out, not_3_out, or_1_out;

  or or_1 (or_1_out, ~Result0, Zero);  // OR_Gate
  not not_1 (not_1_out, 1'b0);
  not not_2 (not_2_out, Zero);
  Multiplexer #(.select(3), .enable("false")) multiplexer_1 (
    .in0(1'b0), .in1(not_1_out), .in2(not_1_out), .in4(Zero), .in5(not_2_out), .in6(Result0), .in7(or_1_out),
    .out(NxtBSrc), .sel(Branch));  // open: in3
  not not_3 (not_3_out, 1'b0);
  Multiplexer #(.select(3), .enable("false")) multiplexer_2 (
    .in0(1'b0), .in1(1'b0), .in2(not_3_out), .in4(1'b0), .in5(1'b0), .in6(1'b0), .in7(1'b0), .out(NxtASrc),
    .sel(Branch));  // open: in3

  // Notes on the sheet:
  //   Branch: pull=down
  //   Zero: pull=down
  //   输入信号
  //   请勿修改引脚名称、电路名称及电路封装外观
  //   不要修改控制信号的编码定义、引脚名称和在布局中的位置。
  //   输出信号
endmodule

module IFU (
  input  [31:0] Initial_Address,
  input  [31:0] Imm,
  input  [31:0] BusA,
  input  CLK,
  input  Reset,
  input  NxtASrc,
  input  NxtBSrc,
  output [31:0] PC
);

  wire [17:2] undriven;
  wire [31:0] adder_1_out, multiplexer_1_out, multiplexer_2_out, multiplexer_3_out;

  Multiplexer #(.width(32), .enable("false")) multiplexer_1 (
    .in0(adder_1_out), .in1(Initial_Address), .out(multiplexer_1_out), .sel(Reset));
  Multiplexer #(.width(32), .enable("false")) multiplexer_2 (
    .in0(PC), .in1(BusA), .out(multiplexer_2_out), .sel(NxtASrc));
  Multiplexer #(.width(32), .enable("false")) multiplexer_3 (
    .in0(32'h4), .in1(Imm), .out(multiplexer_3_out), .sel(NxtBSrc));
  Register #(.width(32), .Select("high")) register_1 (
    .D(multiplexer_1_out), .en(1'b1), .Q(PC), .clk(CLK), .clr(1'b0), .cs(1'b1), .preset(1'b0));
  Adder #(.width(32)) adder_1 (
    .a(multiplexer_2_out), .b(multiplexer_3_out), .out(adder_1_out), .cin(1'b0));  // open: cout
  ROM #(.addrWidth(16), .dataWidth(32), .Select("high")) rom_1 (.addr(undriven), .sel(1'b1));  // open: data

  // Other names for the same wires on the sheet: Init_Addr[31:0] = Initial_Address

  // Notes on the sheet:
  //   Imm: pull=down
  //   NxtASrc: pull=down
  //   NxtBSrc: pull=down
  //   BusA: pull=down
  //   输入信号
  //   请勿修改引脚名称、电路名称及电路封装外观
  //   指令存储器256KB，数据位为32位，地址位为16位。PC寄存器数据宽度32位，片选信号高电平有效
  //   输出信号
  //   contents of rom_1 (hex, n*v repeats v):
  //   256*0 2083 8133 106213 406293 fff06313 4410663 106193 406393 806413 21b5b3 2058063 3a483 42503
  //   a4b5b3 458c63 a3a023 942023 c0006f 610133 fc9ff06f 4181b3 5383b3 540433 fc9ff06f 6f 0 0 413 9117
  //   ffc10113 94000ef 50463 8067 ff010113 100513 112623 74000ef ff010113 812423 912223 15c00413 1212023
  //   112623 c400493 9840913 442783 42703 4a503 440413 e787b3 40f50533 153513 f42223 448493 fa5ff0ef
  //   fd241ce3 100513 f99ff0ef c12083 812403 412483 12903 513 1010113 8067 1ea02e23 6f ff010113 b800513
  //   112623 f7dff0ef 1ea02e23 6f 0 1 1 2 3 5 8 d 15 22 37 59 90 e9 179 262 3db 63d a18 1055 1a6d 2ac2
  //   452f 6ff1 b520 12511 1da31 2ff42 4d973 7d8b5 cb228 148add 213d05 35c7e2 5704e7 8cccc9 e3d1b0 1709e79
  //   2547029 3c50ea2 6197ecb 1 1 deadbeef 395*0 413 9117 ffc10113 ec000ef 50463 8067 ff010113 100513
  //   112623 cc000ef ff010113 19400813 112623 812423 912223 1212023 100793 f82223 f82023 880593 7c80313
  //   100713 19800513 100893 50493 50793 100693 80006f 7a703 d70633 c7a023 478793 70693 feb796e3 117a023
  //   478593 658663 482703 fc9ff06f 11400413 7c40913 100793 c0006f 4a783 448493 42503 440413 40f50533
  //   153513 f4dff0ef fe8912e3 100513 f41ff0ef c12083 812403 412483 12903 513 1010113 8067 18a02823 6f
  //   ff010113 11000513 112623 f25ff0ef 18a02823 6f 0 1 1e 1b3 fdc 6b0d 22caa 90f6f 1f1058 594efd da4f4e
  //   1ca7357 3418be4 527c829 72363ea 8aaf953 93ee7d0 8aaf953 72363ea 527c829 3418be4 1ca7357 da4f4e
  //   594efd 1f1058 90f6f 22caa 6b0d fdc 1b3 1e 1 2 3 4 5 6 7 8 9 a b c d e f 10 11 12 13 14 15 16 17 18
  //   19 1a 1b 1c 1d 1e 1f deadbeef deadbeef 444*0 413 9117 ffc10113 39c000ef 50463 8067 ff010113 100513
  //   112623 380000ef 259693 d506b3 50893 6a803 60513 6c5dc63 261793 f887b3 7a783 fff50613 261613 c88633
  //   140006f fff50513 472783 6b50863 70613 ffc60713 fef846e3 259693 d886b3 251313 f6a023 688633 4a5de63
  //   68713 c0006f 158593 2a58463 72783 70693 470713 fef856e3 f62023 f8a5cee3 58513 106a023 8067 6886b3
  //   6a783 f62023 106a023 8067 251693 d886b3 f6a023 fe9ff06f 58513 fe1ff06f 1ec5da63 fa010113 4812c23
  //   5612023 3812c23 4112e23 4912a23 5212823 5312623 5412423 5512223 3712e23 3912a23 3a12823 3b12623
  //   58c13 60b13 50413 b0613 c0593 40513 ee9ff0ef a12223 fff50c93 159c5663 c8613 c0593 40513 ecdff0ef
  //   a12423 fff50d13 13ac5263 d0613 c0593 40513 eb1ff0ef a12623 fff50d93 fbc5e63 d8613 c0593 40513
  //   e95ff0ef a12823 fff50993 d3c5a63 98613 c0593 40513 e79ff0ef fff50913 50493 b2c5863 90613 c0593 40513
  //   e5dff0ef fff50b93 50a13 97c5663 b8613 c0593 40513 e41ff0ef a12a23 fff50a93 75c5263 a8613 c0593 40513
  //   e25ff0ef fff50693 50713 4dc5063 68613 c0593 40513 e12e23 d12c23 e01ff0ef 50813 c0593 fff50613 40513
  //   180c13 eadff0ef 1812683 1c12703 fcdc44e3 170c13 fb5c42e3 1412783 178c13 f77c4ee3 1a0c13 f52c4ce3
  //   148c13 f33c4ae3 1012783 178c13 f1bc46e3 c12783 178c13 efac42e3 812783 178c13 eb9c4ee3 412783 178c13
  //   e96c4ae3 5c12083 5812403 5412483 5012903 4c12983 4812a03 4412a83 4012b03 3c12b83 3812c03 3412c83
  //   3012d03 2c12d83 6010113 8067 8067 fe010113 1412423 1300613 593 3c000513 812c23 912a23 1212823
  //   1312623 112e23 3c000493 dddff0ef 3c000913 413 1400993 92503 490913 40850533 153513 140413 cddff0ef
  //   ff3414e3 100513 cd1ff0ef 1300613 593 3c000513 d9dff0ef 413 1400913 4a503 448493 40850533 153513
  //   140413 ca1ff0ef ff2414e3 100513 c95ff0ef 1c12083 1812403 1412483 1012903 c12983 812a03 513 2010113
  //   8067 6f ff010113 3bc00513 112623 f31ff0ef 6f 0 2 c e 6 d f 10 a 0 12 b 13 9 1 7 5 4 3 8 11 deadbeef
  //   deadbeef 63658*0 413 9117 ffc10113 39c000ef 50463 8067 ff010113 100513 112623 380000ef 259693 d506b3
  //   50893 6a803 60513 6c5dc63 261793 f887b3 7a783 fff50613 261613 c88633 140006f fff50513 472783 6b50863
  //   70613 ffc60713 fef846e3 259693 d886b3 251313 f6a023 688633 4a5de63 68713 c0006f 158593 2a58463 72783
  //   70693 470713 fef856e3 f62023 f8a5cee3 58513 106a023 8067 6886b3 6a783 f62023 106a023 8067 251693
  //   d886b3 f6a023 fe9ff06f 58513 fe1ff06f 1ec5da63 fa010113 4812c23 5612023 3812c23 4112e23 4912a23
  //   5212823 5312623 5412423 5512223 3712e23 3912a23 3a12823 3b12623 58c13 60b13 50413 b0613 c0593 40513
  //   ee9ff0ef a12223 fff50c93 159c5663 c8613 c0593 40513 ecdff0ef a12423 fff50d13 13a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
endmodule

module IDU (
  input  [31:0] IR,
  input  [31:0] BusW,
  input  [31:0] PC,
  input  [2:0] ExtOp,
  input  RegWr,
  input  ALUASrc,
  input  [1:0] ALUBSrc,
  input  CLK,
  output [31:0] DataA,
  output [31:0] DataB,
  output [31:0] BusA,
  output [31:0] BusB,
  output [6:0] OpCode,
  output [31:0] Imm,
  output [2:0] Funct3,
  output [6:0] Funct7
);

  \立即数扩展器  \u_立即数扩展器_1  (.Instr(IR), .Extop(ExtOp), .imm(Imm));
  RegFile regfile_1 (
    .R1_num(IR[19:15]), .R2_num(IR[24:20]), .Write_Reg_num(IR[11:7]), .Write_Enable(RegWr), .Clock(CLK),
    .Din(BusW), .Reg1Out(BusA), .Reg2Out(BusB));
  Multiplexer #(.select(2), .width(32), .enable("false")) multiplexer_1 (
    .in0(BusB), .in1(32'h4), .in2(Imm), .out(DataB), .sel(ALUBSrc));  // open: in3
  Multiplexer #(.width(32), .enable("false")) multiplexer_2 (.in0(BusA), .in1(PC), .out(DataA), .sel(ALUASrc));

  assign Funct3 = IR[14:12];
  assign Funct7 = IR[31:25];
  assign OpCode = IR[6:0];

  // Other names for the same wires on the sheet: op[6:0] = IR[6:0]

  // Notes on the sheet:
  //   PC: pull=down
  //   ALUASrc: pull=down
  //   ALUBSrc: pull=down
  //   BusW: pull=down
  //   ExtOp: pull=down
  //   RegWr: pull=down
  //   输入信号
  //   为了后续实验中的引用，不要修改ALUASrc、ALUBSrc和EXtOP编码定义。
  //   请勿修改引脚名称、电路名称及电路封装外观
  //   输出信号
  //   修改寄存器堆电路设计，0号寄存器始终为0。
endmodule

module RegFile (
  input  [4:0] R1_num,
  input  [4:0] R2_num,
  input  [4:0] Write_Reg_num,
  input  [31:0] Din,
  input  Write_Enable,
  input  Clock,
  output [31:0] Reg1Out,
  output [31:0] Reg2Out
);

  wire and_1_out, and_2_out, and_3_out, and_4_out, and_5_out, and_6_out, and_7_out, and_8_out, and_9_out,
       and_10_out, and_11_out, and_12_out, and_13_out, and_14_out, and_15_out, and_16_out, and_17_out,
       and_18_out, and_19_out, and_20_out, and_21_out, and_22_out, and_23_out, and_24_out, and_25_out,
       and_26_out, and_27_out, and_28_out, and_29_out, and_30_out, and_31_out, and_32_out, decoder_1_out0,
       decoder_1_out1, decoder_1_out2, decoder_1_out3, decoder_1_out4, decoder_1_out5, decoder_1_out6,
       decoder_1_out7, decoder_1_out8, decoder_1_out9, decoder_1_out10, decoder_1_out11, decoder_1_out12,
       decoder_1_out13, decoder_1_out14, decoder_1_out15, decoder_1_out16, decoder_1_out17, decoder_1_out18,
       decoder_1_out19, decoder_1_out20, decoder_1_out21, decoder_1_out22, decoder_1_out23, decoder_1_out24,
       decoder_1_out25, decoder_1_out26, decoder_1_out27, decoder_1_out28, decoder_1_out29, decoder_1_out30,
       decoder_1_out31;
  wire [31:0] _0_q, _1_q, _2_q, _3_q, _4_q, _5_q, _6_q, _7_q, _8_q, _9_q, _20_q, _21_q, register_1_q,
       register_2_q, register_3_q, register_4_q, register_5_q, register_6_q, register_7_q, register_8_q,
       register_9_q, register_10_q, register_11_q, register_12_q, register_13_q, register_14_q,
       register_15_q, register_16_q, register_17_q, register_18_q, register_19_q, register_20_q;

  Decoder #(.select(5), .enable("false")) decoder_1 (
    .out0(decoder_1_out0), .out1(decoder_1_out1), .out2(decoder_1_out2), .out3(decoder_1_out3),
    .out4(decoder_1_out4), .out5(decoder_1_out5), .out6(decoder_1_out6), .out7(decoder_1_out7),
    .out8(decoder_1_out8), .out9(decoder_1_out9), .out10(decoder_1_out10), .out11(decoder_1_out11),
    .out12(decoder_1_out12), .out13(decoder_1_out13), .out14(decoder_1_out14), .out15(decoder_1_out15),
    .out16(decoder_1_out16), .out17(decoder_1_out17), .out18(decoder_1_out18), .out19(decoder_1_out19),
    .out20(decoder_1_out20), .out21(decoder_1_out21), .out22(decoder_1_out22), .out23(decoder_1_out23),
    .out24(decoder_1_out24), .out25(decoder_1_out25), .out26(decoder_1_out26), .out27(decoder_1_out27),
    .out28(decoder_1_out28), .out29(decoder_1_out29), .out30(decoder_1_out30), .out31(decoder_1_out31),
    .sel(Write_Reg_num));
  and and_1 (and_1_out, Write_Enable, decoder_1_out0);
  and and_2 (and_2_out, decoder_1_out1, Write_Enable);
  and and_3 (and_3_out, Write_Enable, decoder_1_out2);
  and and_4 (and_4_out, decoder_1_out3, Write_Enable);
  and and_5 (and_5_out, decoder_1_out4, Write_Enable);
  and and_6 (and_6_out, Write_Enable, decoder_1_out5);
  and and_7 (and_7_out, decoder_1_out6, Write_Enable);
  and and_8 (and_8_out, decoder_1_out7, Write_Enable);
  and and_9 (and_9_out, Write_Enable, decoder_1_out8);
  and and_10 (and_10_out, Write_Enable, decoder_1_out9);
  and and_11 (and_11_out, Write_Enable, decoder_1_out10);
  and and_12 (and_12_out, Write_Enable, decoder_1_out11);
  and and_13 (and_13_out, decoder_1_out12, Write_Enable);
  and and_14 (and_14_out, decoder_1_out13, Write_Enable);
  and and_15 (and_15_out, decoder_1_out14, Write_Enable);
  and and_16 (and_16_out, decoder_1_out15, Write_Enable);
  and and_17 (and_17_out, Write_Enable, decoder_1_out16);
  and and_18 (and_18_out, Write_Enable, decoder_1_out17);
  and and_19 (and_19_out, decoder_1_out18, Write_Enable);
  and and_20 (and_20_out, Write_Enable, decoder_1_out19);
  and and_21 (and_21_out, decoder_1_out20, Write_Enable);
  and and_22 (and_22_out, decoder_1_out21, Write_Enable);
  and and_23 (and_23_out, decoder_1_out22, Write_Enable);
  and and_24 (and_24_out, decoder_1_out23, Write_Enable);
  and and_25 (and_25_out, decoder_1_out24, Write_Enable);
  and and_26 (and_26_out, Write_Enable, decoder_1_out25);
  and and_27 (and_27_out, decoder_1_out26, Write_Enable);
  and and_28 (and_28_out, decoder_1_out27, Write_Enable);
  and and_29 (and_29_out, Write_Enable, decoder_1_out28);
  and and_30 (and_30_out, decoder_1_out29, Write_Enable);
  and and_31 (and_31_out, Write_Enable, decoder_1_out30);
  and and_32 (and_32_out, decoder_1_out31, Write_Enable);
  Register #(.width(32), .Select("high")) _0 (.D(Din), .en(and_1_out), .Q(_0_q));  // open: clk, clr
  Register #(.width(32), .Select("high")) _1 (
    .D(Din), .en(and_2_out), .Q(_1_q), .clk(Clock), .clr(1'b0), .cs(1'b1), .preset(1'b0));
  Register #(.width(32), .Select("high")) _2 (
    .D(Din), .en(and_3_out), .Q(_2_q), .clk(Clock), .clr(1'b0), .cs(1'b1), .preset(1'b0));
  Register #(.width(32), .Select("high")) _3 (
    .D(Din), .en(and_4_out), .Q(_3_q), .clk(Clock), .clr(1'b0), .cs(1'b1), .preset(1'b0));
  Register #(.width(32), .Select("high")) _4 (
    .D(Din), .en(and_5_out), .Q(_4_q), .clk(Clock), .clr(1'b0), .cs(1'b1), .preset(1'b0));
  Register #(.width(32), .Select("high")) _5 (
    .D(Din), .en(and_6_out), .Q(_5_q), .clk(Clock), .clr(1'b0), .cs(1'b1), .preset(1'b0));
  Register #(.width(32), .Select("high")) _6 (
    .D(Din), .en(and_7_out), .Q(_6_q), .clk(Clock), .clr(1'b0), .cs(1'b1), .preset(1'b0));
  Register #(.width(32), .Select("high")) _7 (
    .D(Din), .en(and_8_out), .Q(_7_q), .clk(Clock), .clr(1'b0), .cs(1'b1), .preset(1'b0));
  Register #(.width(32), .Select("high")) _8 (
    .D(Din), .en(and_9_out), .Q(_8_q), .clk(Clock), .clr(1'b0), .cs(1'b1), .preset(1'b0));
  Register #(.width(32), .Select("high")) _9 (
    .D(Din), .en(and_10_out), .Q(_9_q), .clk(Clock), .clr(1'b0), .cs(1'b1), .preset(1'b0));
  Register #(.width(32), .Select("high")) register_1 (
    .D(Din), .en(and_11_out), .Q(register_1_q), .clk(Clock), .clr(1'b0), .cs(1'b1), .preset(1'b0));
  Register #(.width(32), .Select("high")) register_2 (
    .D(Din), .en(and_12_out), .Q(register_2_q), .clk(Clock), .clr(1'b0), .cs(1'b1), .preset(1'b0));
  Register #(.width(32), .Select("high")) register_3 (
    .D(Din), .en(and_13_out), .Q(register_3_q), .clk(Clock), .clr(1'b0), .cs(1'b1), .preset(1'b0));
  Register #(.width(32), .Select("high")) register_4 (
    .D(Din), .en(and_14_out), .Q(register_4_q), .clk(Clock), .clr(1'b0), .cs(1'b1), .preset(1'b0));
  Register #(.width(32), .Select("high")) register_5 (
    .D(Din), .en(and_15_out), .Q(register_5_q), .clk(Clock), .clr(1'b0), .cs(1'b1), .preset(1'b0));
  Register #(.width(32), .Select("high")) register_6 (
    .D(Din), .en(and_16_out), .Q(register_6_q), .clk(Clock), .clr(1'b0), .cs(1'b1), .preset(1'b0));
  Register #(.width(32), .Select("high")) register_7 (
    .D(Din), .en(and_17_out), .Q(register_7_q), .clk(Clock), .clr(1'b0), .cs(1'b1), .preset(1'b0));
  Register #(.width(32), .Select("high")) register_8 (
    .D(Din), .en(and_18_out), .Q(register_8_q), .clk(Clock), .clr(1'b0), .cs(1'b1), .preset(1'b0));
  Register #(.width(32), .Select("high")) register_9 (
    .D(Din), .en(and_19_out), .Q(register_9_q), .clk(Clock), .clr(1'b0), .cs(1'b1), .preset(1'b0));
  Register #(.width(32), .Select("high")) register_10 (
    .D(Din), .en(and_20_out), .Q(register_10_q), .clk(Clock), .clr(1'b0), .cs(1'b1), .preset(1'b0));
  Register #(.width(32), .Select("high")) _20 (
    .D(Din), .en(and_21_out), .Q(_20_q), .clk(Clock), .clr(1'b0), .cs(1'b1), .preset(1'b0));
  Register #(.width(32), .Select("high")) _21 (
    .D(Din), .en(and_22_out), .Q(_21_q), .clk(Clock), .clr(1'b0), .cs(1'b1), .preset(1'b0));
  Register #(.width(32), .Select("high")) register_11 (
    .D(Din), .en(and_23_out), .Q(register_11_q), .clk(Clock), .clr(1'b0), .cs(1'b1), .preset(1'b0));
  Register #(.width(32), .Select("high")) register_12 (
    .D(Din), .en(and_24_out), .Q(register_12_q), .clk(Clock), .clr(1'b0), .cs(1'b1), .preset(1'b0));
  Register #(.width(32), .Select("high")) register_13 (
    .D(Din), .en(and_25_out), .Q(register_13_q), .clk(Clock), .clr(1'b0), .cs(1'b1), .preset(1'b0));
  Register #(.width(32), .Select("high")) register_14 (
    .D(Din), .en(and_26_out), .Q(register_14_q), .clk(Clock), .clr(1'b0), .cs(1'b1), .preset(1'b0));
  Register #(.width(32), .Select("high")) register_15 (
    .D(Din), .en(and_27_out), .Q(register_15_q), .clk(Clock), .clr(1'b0), .cs(1'b1), .preset(1'b0));
  Register #(.width(32), .Select("high")) register_16 (
    .D(Din), .en(and_28_out), .Q(register_16_q), .clk(Clock), .clr(1'b0), .cs(1'b1), .preset(1'b0));
  Register #(.width(32), .Select("high")) register_17 (
    .D(Din), .en(and_29_out), .Q(register_17_q), .clk(Clock), .clr(1'b0), .cs(1'b1), .preset(1'b0));
  Register #(.width(32), .Select("high")) register_18 (
    .D(Din), .en(and_30_out), .Q(register_18_q), .clk(Clock), .clr(1'b0), .cs(1'b1), .preset(1'b0));
  Register #(.width(32), .Select("high")) register_19 (
    .D(Din), .en(and_31_out), .Q(register_19_q), .clk(Clock), .clr(1'b0), .cs(1'b1), .preset(1'b0));
  Register #(.width(32), .Select("high")) register_20 (
    .D(Din), .en(and_32_out), .Q(register_20_q), .clk(Clock), .clr(1'b0), .cs(1'b1), .preset(1'b0));
  Multiplexer #(.select(5), .width(32), .enable("false")) multiplexer_1 (
    .in0(_0_q), .in1(_1_q), .in2(_2_q), .in3(_3_q), .in4(_4_q), .in5(_5_q), .in6(_6_q), .in7(_7_q),
    .in8(_8_q), .in9(_9_q), .in10(register_1_q), .in11(register_2_q), .in12(register_3_q),
    .in13(register_4_q), .in14(register_5_q), .in15(register_6_q), .in16(register_7_q), .in17(register_8_q),
    .in18(register_9_q), .in19(register_10_q), .in20(_20_q), .in21(_21_q), .in22(register_11_q),
    .in23(register_12_q), .in24(register_13_q), .in25(register_14_q), .in26(register_15_q),
    .in27(register_16_q), .in28(register_17_q), .in29(register_18_q), .in30(register_19_q),
    .in31(register_20_q), .out(Reg1Out), .sel(R1_num));
  Multiplexer #(.select(5), .width(32), .enable("false")) multiplexer_2 (
    .in0(_0_q), .in1(_1_q), .in2(_2_q), .in3(_3_q), .in4(_4_q), .in5(_5_q), .in6(_6_q), .in7(_7_q),
    .in8(_8_q), .in9(_9_q), .in10(register_1_q), .in11(register_2_q), .in12(register_3_q),
    .in13(register_4_q), .in14(register_5_q), .in15(register_6_q), .in16(register_7_q), .in17(register_8_q),
    .in18(register_9_q), .in19(register_10_q), .in20(_20_q), .in21(_21_q), .in22(register_11_q),
    .in23(register_12_q), .in24(register_13_q), .in25(register_14_q), .in26(register_15_q),
    .in27(register_16_q), .in28(register_17_q), .in29(register_18_q), .in30(register_19_q),
    .in31(register_20_q), .out(Reg2Out), .sel(R2_num));

  // Other names for the same wires on the sheet: CLK = Clock; RA[4:0] = R1_num; RB[4:0] = R2_num; RDA[31:0] = Reg1Out;
  //   RDB[31:0] = Reg2Out; RW[4:0] = Write_Reg_num; WE = Write_Enable

  // Notes on the sheet:
  //   输入引脚
  //   请勿修改引脚名称、电路名称及电路封装外观
  //   提示：使用译码器、多路选择器和32位寄存器及逻辑门实现寄存器堆，禁止直接使用存储器组件。
  //   输出引脚
endmodule

module \立即数扩展器  (
  input  [31:0] Instr,
  input  [2:0] Extop,
  output [31:0] imm
);

  wire [11:0] bit_extender_4_out;
  wire [19:0] bit_extender_1_out, bit_extender_2_out, bit_extender_3_out;

  assign bit_extender_1_out = {{19{Instr[31]}}, Instr[31]};  // Bit_Extender bit_extender_1
  assign bit_extender_2_out = {{19{Instr[31]}}, Instr[31]};  // Bit_Extender bit_extender_2
  assign bit_extender_3_out = {{19{Instr[31]}}, Instr[31]};  // Bit_Extender bit_extender_3
  assign bit_extender_4_out = {{11{Instr[31]}}, Instr[31]};  // Bit_Extender bit_extender_4
  Multiplexer #(.select(3), .width(32), .enable("false")) multiplexer_1 (
    .in0({bit_extender_1_out, Instr[31:20]}), .in1({Instr[31:12], {12{1'b0}}}),
    .in2({bit_extender_2_out, Instr[31:25], Instr[11:7]}),
    .in3({bit_extender_3_out, Instr[7], Instr[30:25], Instr[11:8], 1'b0}),
    .in4({bit_extender_4_out, Instr[19:12], Instr[20], Instr[30:21], 1'b0}), .out(imm), .sel(Extop));  // open: in5, in6, in7

  // Notes on the sheet:
  //   Instr: pull=down
  //   Extop: pull=down
  //   B
  //   J
  //   输入引脚
  //   I
  //   U
  //   S
  //   输出引脚
endmodule

module DataRAM (
  input  CLK,
  input  CLR,
  input  WE,
  input  [2:0] MemOp,
  input  [17:0] Addr,
  input  [31:0] Din,
  output AlignErr,
  output [31:0] DataOut
);

  wire and_1_out, and_2_out, and_3_out, and_4_out, and_5_out, and_6_out, and_7_out, and_8_out, and_9_out,
       and_10_out, and_11_out, and_12_out, and_13_out, and_14_out, and_15_out, and_16_out, Byte1Sel, MemOPwe,
       nor_1_out;
  wire [3:0] Byte0Sel;
  wire [7:0] multiplexer_1_out, multiplexer_2_out, multiplexer_3_out, multiplexer_4_out, multiplexer_5_out,
       ram_4_data;
  wire [31:0] bit_extender_3_out, bit_extender_4_out;
  wire [31:8] bit_extender_1_out, bit_extender_2_out, ram_3_data;

  and and_1 (and_1_out, WE, MemOPwe);
  nor nor_1 (nor_1_out, MemOp[0], MemOp[1], MemOp[2]);
  and and_2 (and_2_out, MemOp[0], ~MemOp[1], MemOp[2]);  // AND_Gate
  and and_3 (and_3_out, ~MemOp[0], MemOp[1], MemOp[2]);  // AND_Gate
  and and_4 (and_4_out, MemOp[0], ~MemOp[1]);  // AND_Gate
  and and_5 (and_5_out, ~MemOp[0], MemOp[1]);  // AND_Gate
  and and_6 (and_6_out, ~Addr[1], ~Addr[0]);  // AND_Gate
  and and_7 (and_7_out, ~Addr[1], Addr[0]);  // AND_Gate
  and and_8 (and_8_out, Addr[1], ~Addr[0]);  // AND_Gate
  and and_9 (and_9_out, Addr[1], Addr[0]);
  Multiplexer #(.select(2), .width(8), .enable("false")) multiplexer_1 (
    .in0(Din[7:0]), .in2(Din[15:8]), .in3(Din[31:24]), .out(multiplexer_1_out),
    .sel({Byte0Sel[2], Byte0Sel[0]}));  // open: in1
  RAM #(.addrWidth(16), .bus("separate"), .Select("high")) ram_1 (
    .addr(Addr[17:2]), .din(multiplexer_1_out), .data(ram_3_data[31:24]), .str(and_1_out), .sel(Byte0Sel[3]),
    .clk(CLK), .clr(CLR));  // open: ld
  Multiplexer #(.width(8), .enable("false")) multiplexer_2 (
    .in0(Din[7:0]), .in1(Din[23:16]), .out(multiplexer_2_out), .sel(Byte0Sel[0]));
  or or_1 (MemOPwe, nor_1_out, and_2_out, and_3_out);
  and and_10 (and_10_out, nor_1_out, and_6_out);
  and and_11 (and_11_out, and_5_out, and_6_out);
  and and_12 (and_12_out, and_4_out, and_6_out);
  and and_13 (and_13_out, and_4_out, and_7_out);
  and and_14 (and_14_out, and_5_out, and_8_out);
  and and_15 (and_15_out, and_8_out, and_4_out);
  and and_16 (and_16_out, and_9_out, and_4_out);
  RAM #(.addrWidth(16), .bus("separate"), .Select("high")) ram_2 (
    .addr(Addr[17:2]), .din(multiplexer_2_out), .data(ram_3_data[23:16]), .str(and_1_out), .sel(Byte0Sel[2]),
    .clk(CLK), .clr(CLR));  // open: ld
  Multiplexer #(.width(8), .enable("false")) multiplexer_3 (
    .in0(Din[7:0]), .in1(Din[15:8]), .out(multiplexer_3_out), .sel(Byte0Sel[0]));
  or or_2 (Byte0Sel[3], and_10_out, and_14_out, and_16_out);
  or or_3 (Byte0Sel[2], and_10_out, and_14_out, and_15_out);
  or or_4 (Byte0Sel[1], and_10_out, and_13_out, and_11_out);
  or or_5 (Byte0Sel[0], and_10_out, and_12_out, and_11_out);
  RAM #(.addrWidth(16), .bus("separate"), .Select("high")) ram_3 (
    .addr(Addr[17:2]), .din(multiplexer_3_out), .data(ram_3_data[15:8]), .str(and_1_out), .sel(Byte0Sel[1]),
    .clk(CLK), .clr(CLR));  // open: ld
  and and_17 (Byte1Sel, ~Byte0Sel[1], Byte0Sel[3]);  // AND_Gate
  Multiplexer #(.width(8), .enable("false")) multiplexer_4 (
    .in0(ram_3_data[15:8]), .in1(ram_3_data[31:24]), .out(multiplexer_4_out), .sel(Byte1Sel));
  nor nor_2 (AlignErr, Byte0Sel[3], Byte0Sel[2], Byte0Sel[0], Byte0Sel[1]);
  RAM #(.addrWidth(16), .bus("separate"), .Select("high")) ram_4 (
    .addr(Addr[17:2]), .din(Din[7:0]), .data(ram_4_data), .str(and_1_out), .sel(Byte0Sel[0]), .clk(CLK),
    .clr(CLR));  // open: ld
  assign bit_extender_1_out = {{16{1'b0}}, multiplexer_4_out};  // Bit_Extender bit_extender_1
  assign bit_extender_2_out = {{16{multiplexer_4_out[7]}}, multiplexer_4_out};  // Bit_Extender bit_extender_2
  Multiplexer #(.select(4), .width(8), .enable("false")) multiplexer_5 (
    .in1(ram_4_data), .in2(ram_3_data[15:8]), .in3(ram_4_data), .in4(ram_3_data[23:16]),
    .in8(ram_3_data[31:24]), .in12(ram_3_data[23:16]), .in15(ram_4_data), .out(multiplexer_5_out),
    .sel(Byte0Sel));  // open: in0, in5, in6, in7, in9, in10, in11, in13, in14
  assign bit_extender_3_out = {{24{1'b0}}, multiplexer_5_out};  // Bit_Extender bit_extender_3
  assign bit_extender_4_out = {{24{multiplexer_5_out[7]}}, multiplexer_5_out};  // Bit_Extender bit_extender_4
  Multiplexer #(.select(3), .width(32), .enable("false")) multiplexer_6 (
    .in0({ram_3_data, multiplexer_5_out}), .in1(bit_extender_3_out),
    .in2({bit_extender_1_out, multiplexer_5_out}), .in4({ram_3_data, multiplexer_5_out}),
    .in5(bit_extender_4_out), .in6({bit_extender_2_out, multiplexer_5_out}), .out(DataOut), .sel(MemOp));  // open: in3, in7

  // Other names for the same wires on the sheet: ramAddr[15:0] = Addr[17:2];
  //   Byte3Sel[1:0] = {Byte0Sel[2], Byte0Sel[0]}; SEL0 = Byte0Sel[0]; SEL1 = Byte0Sel[1]; SEL2 = Byte0Sel[2];
  //   SEL3 = Byte0Sel[3]; Dout[31:0] = DataOut

  // Notes on the sheet:
  //   输入引脚
  //   请勿修改引脚名称、电路名称及电路封装外观
  //   为了后续实验中的引用，不要修改MemOp的编码定义、引脚名称和在布局中的位置。
  //   32位数据存储器，按字节分4片存储，可按照字节、半字和字进行存储；读取字节或半字时，支持0扩展和符号位扩展。
  //   输出引脚
endmodule

module ALU (
  input  [3:0] ALUctr,
  input  [31:0] A,
  input  [31:0] B,
  output Zero,
  output [31:0] S
);

  wire adder32_1_cf, adder32_1_of, adder32_1_sf, aluctrl_1_alctr, aluctrl_1_sftctr, aluctrl_1_sigctr,
       aluctrl_1_subctr, multiplexer_2_out, xor_3_out;
  wire [2:0] aluctrl_1_opctr;
  wire [31:0] adder32_1_s, and_1_out, bit_extender_1_out, bit_extender_2_out, or_1_out, shifter32_1_dataout,
       xor_1_out, xor_2_out;

  assign bit_extender_1_out = {{31{aluctrl_1_subctr}}, aluctrl_1_subctr};  // Bit_Extender bit_extender_1
  assign xor_1_out = B ^ bit_extender_1_out;  // XOR_Gate xor_1, 32 bits wide
  assign and_1_out = A & B;  // AND_Gate and_1, 32 bits wide
  assign or_1_out = A | B;  // OR_Gate or_1, 32 bits wide
  assign xor_2_out = A ^ B;  // XOR_Gate xor_2, 32 bits wide
  Adder32 adder32_1 (
    .CF(adder32_1_cf), .OF(adder32_1_of), .SF(adder32_1_sf), .ZF(Zero), .X(A), .Y(xor_1_out),
    .Cin(aluctrl_1_subctr), .S(adder32_1_s));  // open: Cout
  Shifter32 shifter32_1 (
    .DataIn(A), .shamt(B[4:0]), .L_R(aluctrl_1_sftctr), .A_L(aluctrl_1_alctr), .DataOut(shifter32_1_dataout));
  xor xor_3 (xor_3_out, adder32_1_of, adder32_1_sf);
  // Probe on A
  // Probe on B
  // Probe on S
  Multiplexer #(.select(3), .width(32), .enable("false")) multiplexer_1 (
    .in0(adder32_1_s), .in1(and_1_out), .in2(or_1_out), .in3(xor_2_out), .in4(shifter32_1_dataout), .in5(B),
    .in6(bit_extender_2_out), .out(S), .sel(aluctrl_1_opctr));  // open: in7
  ALUctrl aluctrl_1 (
    .SUBctr(aluctrl_1_subctr), .SFTctr(aluctrl_1_sftctr), .SIGctr(aluctrl_1_sigctr), .ALctr(aluctrl_1_alctr),
    .OPctr(aluctrl_1_opctr), .ALUctr(ALUctr));
  Multiplexer #(.enable("false")) multiplexer_2 (
    .in0(adder32_1_cf), .in1(xor_3_out), .out(multiplexer_2_out), .sel(aluctrl_1_sigctr));
  assign bit_extender_2_out = {{31{1'b0}}, multiplexer_2_out};  // Bit_Extender bit_extender_2

  // Other names for the same wires on the sheet: Result[31:0] = S

  // Notes on the sheet:
  //   A: pull=down
  //   ALUctr: pull=down
  //   B: pull=down
  //   输入引脚
  //   请勿修改引脚名称、电路名称及电路封装外观
  //   提示：使用32位并行加法器子电路、桶形移位器、ALU控制子电路实现32位ALU
  //   功能说明:32位ALU，输入32位操作数A、B，4位控制信号ALUctr，输出32位结果Reseult和1位Zero标志位
  //   输出引脚
  //   操作数和结果
endmodule

module ALUctrl (
  input  [3:0] ALUctr,
  output SUBctr,
  output SFTctr,
  output SIGctr,
  output ALctr,
  output [2:0] OPctr
);

  wire and_2_out, and_3_out;

  Multiplexer #(.select(4), .width(3), .enable("false")) multiplexer_1 (
    .in0(3'b000), .in1(3'b100), .in2(3'b110), .in3(3'b110), .in4(3'b011), .in5(3'b100), .in6(3'b010),
    .in7(3'b001), .in8(3'b000), .in9(3'b000), .in10(3'b000), .in11(3'b000), .in12(3'b000), .in13(3'b100),
    .in14(3'b000), .in15(3'b101), .out(OPctr), .sel(ALUctr));
  and and_1 (SIGctr, ~ALUctr[3], ~ALUctr[2], ALUctr[1], ~ALUctr[0]);  // AND_Gate
  and and_2 (and_2_out, ~ALUctr[3], ~ALUctr[2], ALUctr[1], ALUctr[0]);  // AND_Gate
  and and_3 (and_3_out, ALUctr[3], ~ALUctr[2], ~ALUctr[1], ~ALUctr[0]);  // AND_Gate
  and and_4 (SFTctr, ~ALUctr[3], ~ALUctr[2], ~ALUctr[1], ALUctr[0]);  // AND_Gate
  and and_5 (ALctr, ALUctr[3], ALUctr[2], ~ALUctr[1], ALUctr[0]);  // AND_Gate
  or or_1 (SUBctr, SIGctr, and_2_out, and_3_out);

  // Other names for the same wires on the sheet: LRctr = SFTctr

  // Notes on the sheet:
  //   输入引脚
  //   ALU操作控制信号生成部件
  //   输出引脚
endmodule

module Adder32 (
  input  Cin,
  input  [31:0] X,
  input  [31:0] Y,
  output CF,
  output Cout,
  output OF,
  output SF,
  output [31:0] S,
  output ZF
);

  wire adder16_2_c16, and_1_out, and_2_out, not_1_out, not_2_out, not_3_out, or_3_out, or_4_out;
  wire [3:0] or_1_out, or_2_out;

  Adder16 adder16_1 (.X(X[31:16]), .Y(Y[31:16]), .C0(adder16_2_c16), .S(S[31:16]), .C16(Cout));  // open: Pg, Gg
  assign or_1_out = S[19:16] | S[23:20] | S[27:24] | S[31:28];  // OR_Gate or_1, 4 bits wide
  assign or_2_out = S[3:0] | S[7:4] | S[11:8] | S[15:12];  // OR_Gate or_2, 4 bits wide
  or or_3 (or_3_out, or_1_out[0], or_1_out[1], or_1_out[2], or_1_out[3]);
  or or_4 (or_4_out, or_2_out[0], or_2_out[1], or_2_out[2], or_2_out[3]);
  Adder16 adder16_2 (.X(X[15:0]), .Y(Y[15:0]), .C0(Cin), .S(S[15:0]), .C16(adder16_2_c16));  // open: Pg, Gg
  nor nor_1 (ZF, or_3_out, or_4_out);
  // Probe on X
  // Probe on Y
  // Probe on S
  xor xor_1 (CF, Cout, Cin);
  not not_1 (not_1_out, S[31]);
  not not_2 (not_2_out, X[31]);
  not not_3 (not_3_out, Y[31]);
  and and_1 (and_1_out, not_1_out, X[31], Y[31]);
  and and_2 (and_2_out, not_2_out, S[31], not_3_out);
  or or_5 (OF, and_1_out, and_2_out);

  assign SF = S[31];

  // Other names for the same wires on the sheet: S0[15:0] = S[15:0]; S1[15:0] = S[31:16]; X1[15:0] = X[31:16];
  //   Y1[15:0] = Y[31:16]

  // Notes on the sheet:
  //   Y: pull=down
  //   Cin: pull=down
  //   X: pull=down
  //   输入引脚区
  //   输出引脚区
  //   请勿修改引脚名称、电路名称及电路封装外观
  //   提示：使用16位并行加法器子电路实现32位快速加法器
  //   功能说明:32位Adder  S=X+Y，Cout为最高位进位位，Cin为进位输入， S为和，溢出OF、进位CF、零ZF、符号SF。
  //   +
  //   =
  //   无符号加法
endmodule

// 移位器
module Shifter32 (
  input  [4:0] shamt,
  input  L_R,
  input  A_L,
  input  [31:0] DataIn,
  output [31:0] DataOut
);

  wire [0:0] and_1_out;
  wire [1:1] and_3_out, and_4_out;
  wire [3:3] and_5_out, and_6_out;
  wire [7:0] multiplexer_3_out;
  wire [7:7] and_7_out;
  wire [15:15] and_9_out, and_10_out;
  wire [31:0] multiplexer_1_out, multiplexer_2_out, multiplexer_3_out_2, multiplexer_4_out;
  wire [31:31] and_2_out;

  and and_1 (and_1_out[0], A_L, DataIn[31]);
  and and_2 (and_2_out[31], DataIn[31], A_L);
  Multiplexer #(.select(2), .width(32), .enable("false")) multiplexer_1 (
    .in0(DataIn), .in1(DataIn), .in2({and_2_out[31], DataIn[31:1]}), .in3({DataIn[30:0], and_1_out[0]}),
    .out(multiplexer_1_out), .sel({shamt[0], L_R}));
  and and_3 (and_3_out[1], A_L, multiplexer_1_out[31]);
  and and_4 (and_4_out[1], multiplexer_1_out[31], A_L);
  Multiplexer #(.select(2), .width(32), .enable("false")) multiplexer_2 (
    .in0(multiplexer_1_out), .in1(multiplexer_1_out), .in2({{2{and_4_out[1]}}, multiplexer_1_out[31:2]}),
    .in3({multiplexer_1_out[29:0], {2{and_3_out[1]}}}), .out(multiplexer_2_out), .sel({shamt[1], L_R}));
  and and_5 (and_5_out[3], A_L, multiplexer_2_out[31]);
  and and_6 (and_6_out[3], multiplexer_2_out[31], A_L);
  Multiplexer #(.select(2), .width(32), .enable("false")) multiplexer_3 (
    .in0(multiplexer_2_out), .in1(multiplexer_2_out), .in2({{4{and_6_out[3]}}, multiplexer_2_out[31:4]}),
    .in3({multiplexer_2_out[27:0], {4{and_5_out[3]}}}), .out({multiplexer_3_out_2[23:0], multiplexer_3_out}),
    .sel({shamt[2], L_R}));
  and and_7 (and_7_out[7], A_L, multiplexer_3_out_2[23]);
  and and_8 (multiplexer_3_out_2[31], multiplexer_3_out_2[23], A_L);
  Multiplexer #(.select(2), .width(32), .enable("false")) multiplexer_4 (
    .in0({multiplexer_3_out_2[23:0], multiplexer_3_out}),
    .in1({multiplexer_3_out_2[23:0], multiplexer_3_out}),
    .in2({{8{multiplexer_3_out_2[31]}}, multiplexer_3_out_2[23:0]}),
    .in3({multiplexer_3_out_2[15:0], multiplexer_3_out, {8{and_7_out[7]}}}), .out(multiplexer_4_out),
    .sel({shamt[3], L_R}));
  and and_9 (and_9_out[15], A_L, multiplexer_4_out[31]);
  and and_10 (and_10_out[15], multiplexer_4_out[31], A_L);
  Multiplexer #(.select(2), .width(32), .enable("false")) multiplexer_5 (
    .in0(multiplexer_4_out), .in1(multiplexer_4_out), .in2({{16{and_10_out[15]}}, multiplexer_4_out[31:16]}),
    .in3({multiplexer_4_out[15:0], {16{and_9_out[15]}}}), .out(DataOut), .sel({shamt[4], L_R}));

  // Other names for the same wires on the sheet: Din[31:0] = DataIn; Left_Right = L_R; Arth_Logic = A_L;
  //   Dout[31:0] = DataOut

  // Notes on the sheet:
  //   L/R,A/L: 00逻辑右移，01算术右移，10逻辑左移，11：循环左移
  //   输入引脚
  //   请勿修改引脚名称、电路名称及电路封装外观
  //   提示：使用多路选择器、逻辑门实现32位桶形移位器，禁止直接使用移位器组件。
  //   1
  //   对选择器，00/01都不移动；10右移，11左移
  //   输出引脚
  //   2
  //   4
  //   8
  //   16
endmodule

module Adder16 (
  input  C0,
  input  [15:0] X,
  input  [15:0] Y,
  output C16,
  output Pg,
  output Gg,
  output [15:0] S
);

  wire cla4_1_gg, cla4_1_pg, cla4_2_gg, cla4_2_pg, cla4_3_gg, cla4_3_pg, cla4_4_gg, cla4_4_pg, clu4_1_c1,
       clu4_1_c2, clu4_1_c3;

  CLA4 cla4_1 (
    .X(X[15:12]), .F(S[15:12]), .Y(Y[15:12]), .Pg(cla4_1_pg), .Cin(clu4_1_c3), .Gg(cla4_1_gg));  // open: Cout
  CLA4 cla4_2 (.X(X[11:8]), .F(S[11:8]), .Y(Y[11:8]), .Pg(cla4_2_pg), .Cin(clu4_1_c2), .Gg(cla4_2_gg));  // open: Cout
  CLU4 clu4_1 (
    .P0(cla4_4_pg), .P1(cla4_3_pg), .P2(cla4_2_pg), .P3(cla4_1_pg), .C1(clu4_1_c1), .C3(clu4_1_c3),
    .G0(cla4_4_gg), .G1(cla4_3_gg), .G2(cla4_2_gg), .G3(cla4_1_gg), .C2(clu4_1_c2), .C4(C16), .C0(C0),
    .Pg(Pg), .Gg(Gg));
  CLA4 cla4_3 (.X(X[7:4]), .F(S[7:4]), .Y(Y[7:4]), .Pg(cla4_3_pg), .Cin(clu4_1_c1), .Gg(cla4_3_gg));  // open: Cout
  CLA4 cla4_4 (.X(X[3:0]), .F(S[3:0]), .Y(Y[3:0]), .Pg(cla4_4_pg), .Cin(C0), .Gg(cla4_4_gg));  // open: Cout
  // Probe on X
  // Probe on Y
  // Probe on S

  // Notes on the sheet:
  //   Y: pull=down
  //   C0: pull=down
  //   X: pull=down
  //   输入引脚区
  //   请勿修改引脚名称、电路名称及电路封装外观
  //   提示：使用4位先行进位加法器和CLU子电路实现16位并行加法器
  //   功能说明:16位Adder  S=X+Y，C16为最高位进位位，C0为进位输入， Pg、Gg为成组进位生成传递函数
  //   输出引脚区
  //   +
  //   =
  //   无符号加法
endmodule

module CLA4 (
  input  [3:0] X,
  input  [3:0] Y,
  input  Cin,
  output [3:0] F,
  output Cout,
  output Pg,
  output Gg
);

  wire clu4_1_c1, clu4_1_c2, clu4_1_c3, fa_1_g, fa_1_p, fa_2_g, fa_2_p, fa_3_g, fa_3_p, fa_4_g, fa_4_p;

  Hex_Digit_Display hex_digit_display_1 (.value(X));  // open: dp
  FA fa_1 (.A(X[3]), .F(F[3]), .B(Y[3]), .P(fa_1_p), .Cin(clu4_1_c3), .G(fa_1_g));
  Hex_Digit_Display hex_digit_display_2 (.value(Y));  // open: dp
  FA fa_2 (.A(X[1]), .F(F[1]), .B(Y[1]), .P(fa_2_p), .Cin(clu4_1_c1), .G(fa_2_g));
  FA fa_3 (.A(X[2]), .F(F[2]), .B(Y[2]), .P(fa_3_p), .Cin(clu4_1_c2), .G(fa_3_g));
  Hex_Digit_Display hex_digit_display_3 (.value(F));  // open: dp
  CLU4 clu4_1 (
    .P0(fa_4_p), .P1(fa_2_p), .P2(fa_3_p), .P3(fa_1_p), .C1(clu4_1_c1), .C3(clu4_1_c3), .G0(fa_4_g),
    .G1(fa_2_g), .G2(fa_3_g), .G3(fa_1_g), .C2(clu4_1_c2), .C4(Cout), .C0(Cin), .Pg(Pg), .Gg(Gg));
  FA fa_4 (.A(X[0]), .F(F[0]), .B(Y[0]), .P(fa_4_p), .Cin(Cin), .G(fa_4_g));

  // Other names for the same wires on the sheet: Z[3:0] = F

  // Notes on the sheet:
  //   +
  //   =
  //   输出
  //   输入
  //   请勿修改引脚名称、电路名称及电路封装外观
  //   提示：使用全加器和CLU子电路实现四位先行进位加法器CLA4
endmodule

module CLU4 (
  input  P0,
  input  P1,
  input  P2,
  input  P3,
  input  G0,
  input  G1,
  input  G2,
  input  G3,
  input  C0,
  output C1,
  output C3,
  output C2,
  output C4,
  output Pg,
  output Gg
);

  wire and_1_out, and_2_out, and_3_out, and_4_out, and_5_out, and_6_out, and_7_out, and_8_out, and_9_out,
       and_10_out;

  and and_1 (and_1_out, C0, P0);
  and and_2 (and_2_out, G0, P1);
  and and_3 (and_3_out, G1, P2);
  and and_4 (and_4_out, G2, P3);
  and and_5 (and_5_out, and_1_out, P1);
  and and_6 (and_6_out, and_2_out, P2);
  and and_7 (and_7_out, and_3_out, P3);
  or or_1 (C1, and_1_out, G0);
  or or_2 (C2, and_2_out, G1, and_5_out);
  and and_8 (and_8_out, and_5_out, P2);
  and and_9 (and_9_out, and_6_out, P3);
  and and_10 (and_10_out, and_8_out, P3);
  and and_11 (Pg, P0, P1, P2, P3);
  or or_3 (C3, and_3_out, and_6_out, and_8_out, G2);
  or or_4 (Gg, and_4_out, and_7_out, and_9_out, G3);
  or or_5 (C4, and_4_out, and_7_out, and_9_out, and_10_out, G3);

  // Notes on the sheet:
  //   输入引脚
  //   请勿修改引脚名称、电路名称及电路封装外观
  //   提示：使用逻辑门电路实现4位四位先行进位部件CLU，Pg、Gg为成组进位生成传递函数
  //   输出引脚
endmodule

module FA (
  input  A,
  input  B,
  input  Cin,
  output F,
  output P,
  output G
);

  wire xor_1_out;

  and and_1 (G, A, B);
  xor xor_1 (xor_1_out, A, B);
  or or_1 (P, A, B);
  xor xor_2 (F, xor_1_out, Cin);

  // Notes on the sheet:
  //   输入引脚
  //   请勿修改引脚名称、电路名称及电路封装外观
  //   输出引脚
endmodule
