// Logisim project lab6.1.circ as structural Verilog: 1 circuit, main circuit 控制器
module \控制器  (
  input  [6:0] opcode,
  input  [2:0] funct3,
  input  [6:0] funct7,
  output [2:0] ExtOp,
  output RegWr,
  output [2:0] BandJ,
  output ALUASrc,
  output [1:0] ALUBSrc,
  output [3:0] ALUctr,
  output MemtoReg,
  output [2:0] MemOp,
  output MemWr
);

  wire and_1_out, and_2_out, I_TYPE_ALU_out, Jalr_out, or_11_out, R_TYPE_out, U_auipc_out;
  wire [1:1] not_1_out;
  wire [2:0] multiplexer_1_out, U_lui_out;

  and R_TYPE (R_TYPE_out, ~opcode[6], opcode[5], opcode[4], ~opcode[3], ~opcode[2], opcode[1], opcode[0]);  // AND_Gate
  and I_TYPE_ALU (I_TYPE_ALU_out, ~opcode[6], ~opcode[5], opcode[4], ~opcode[3], ~opcode[2], opcode[1], opcode[0]);  // AND_Gate
  and U_lui (U_lui_out[0], ~opcode[6], opcode[5], opcode[4], ~opcode[3], opcode[2], opcode[1], opcode[0]);  // AND_Gate
  and load (MemtoReg, ~opcode[6], ~opcode[5], ~opcode[4], ~opcode[3], ~opcode[2], opcode[1], opcode[0]);  // AND_Gate
  and Store (MemWr, ~opcode[6], opcode[5], ~opcode[4], ~opcode[3], ~opcode[2], opcode[1], opcode[0]);  // AND_Gate
  and B_TYPE (BandJ[2], opcode[6], opcode[5], ~opcode[4], ~opcode[3], ~opcode[2], opcode[1], opcode[0]);  // AND_Gate
  and J_TYPE (ExtOp[2], opcode[6], opcode[5], ~opcode[4], opcode[3], opcode[2], opcode[1], opcode[0]);  // AND_Gate
  and U_auipc (U_auipc_out, ~opcode[6], ~opcode[5], opcode[4], ~opcode[3], opcode[2], opcode[1], opcode[0]);  // AND_Gate
  and Jalr (Jalr_out, opcode[6], opcode[5], ~opcode[4], ~opcode[3], opcode[2], opcode[1], opcode[0]);  // AND_Gate
  or or_1 (U_lui_out[1], U_auipc_out, ExtOp[2], MemtoReg, MemWr, Jalr_out);
  and and_1 (and_1_out, funct3[0], BandJ[2]);
  and and_2 (and_2_out, funct3[2], BandJ[2]);
  or or_2 (U_lui_out[2], I_TYPE_ALU_out, R_TYPE_out);
  or or_3 (BandJ[0], ExtOp[2], and_1_out);
  or or_4 (BandJ[1], Jalr_out, and_2_out);
  or or_5 (RegWr, Jalr_out, R_TYPE_out, I_TYPE_ALU_out, U_lui_out[0], MemtoReg, ExtOp[2], U_auipc_out);
  or or_6 (ALUASrc, ExtOp[2], U_auipc_out, Jalr_out);
  not not_1 (not_1_out[1], 1'b0);
  or or_7 (ALUBSrc[0], ExtOp[2], Jalr_out);
  or or_8 (ALUBSrc[1], I_TYPE_ALU_out, MemWr, MemtoReg, U_lui_out[0], U_auipc_out);
  or or_9 (ExtOp[0], U_auipc_out, U_lui_out[0], BandJ[2]);
  or or_10 (ExtOp[1], BandJ[2], MemWr);
  Multiplexer #(.select(3), .width(3), .enable("false")) multiplexer_1 (
    .in0(3'b101), .in1(3'b110), .in2(3'b000), .in4(3'b001), .in5(3'b010), .out(multiplexer_1_out),
    .sel(funct3));  // open: in3, in6, in7
  Multiplexer #(.select(4), .width(4), .enable("false")) multiplexer_2 (
    .in0(4'b0000), .in1(4'b1111), .in2(4'b0000), .in4({funct7[5], funct3}),
    .in8({2'b00, not_1_out[1], funct3[1]}), .out(ALUctr), .sel({BandJ[2], U_lui_out}));  // open: in3, in5, in6, in7, in9, in10, in11, in12, in13, in14, in15
  or or_11 (or_11_out, MemWr, MemtoReg);
  Multiplexer #(.width(3), .enable("false")) multiplexer_3 (
    .in0(3'b000), .in1(multiplexer_1_out), .out(MemOp), .sel(or_11_out));

  // Notes on the sheet:
  //   输入引脚
  //   请勿修改引脚名称、电路名称及电路封装外观
  //   提示：根据指令种类，把7位指令code用一位指令类型标志位来表示，再通过功能码来区分具体指令，生成控制信号。
  //   输出引脚
  //   R
  //   I-TYPE
  //   U
  //   S
  //   load
  //   func3
endmodule
